// Logisim project triangler_rasterizer.circ as structural Verilog: 1 circuit, main circuit main
module main (
);

  wire comparator_1_gt, d_ff_1_q;
  wire [7:0] counter_1_q, fptoint_1_p2, fptoint_2_p2, fptoint_3_p2, fptoint_4_p1, fptoint_5_p1, fptoint_6_p1,
       fptoint_6_p2, multiplexer_1_out, multiplexer_2_out, multiplexer_3_out, multiplexer_4_out,
       multiplexer_5_out, multiplexer_6_out, multiplexer_7_out, xLeft_q;
  wire [15:0] fpdivider_1_out, fpdivider_2_out, fpdivider_3_out, fpmultiplier_1_out, fpmultiplier_3_out,
       fpmultiplier_4_out, fpmultiplier_5_out, fpmultiplier_6_out, fpmultiplier_7_out, fpmultiplier_8_out,
       fpmultiplier_9_out, fpsubtractor_1_out, fpsubtractor_2_out, fpsubtractor_3_out, fpsubtractor_4_out,
       fpsubtractor_5_out, fpsubtractor_6_out, fpsubtractor_7_out, fpsubtractor_8_out, fpsubtractor_9_out,
       fpsubtractor_10_out, fpsubtractor_11_out, fpsubtractor_12_out, inttofp_1_p2, inttofp_1_p3,
       register_1_q, register_2_q, register_3_q, register_4_q, register_5_q, register_6_q;

  // IntToFP #(.fpwidth(16), .width(16)) inttofp_1: pin names not known; wires that end beside it: 16'hf00, inttofp_1_p2, inttofp_1_p3
  Register #(.width(16)) register_1 (.Q(register_1_q));  // open: D, en, clk, clr
  Register #(.width(16)) register_2 (.Q(register_2_q));  // open: D, en, clk, clr
  Register #(.width(16)) register_3 (.Q(register_3_q));  // open: D, en, clk, clr
  Register #(.width(16)) register_4 (.Q(register_4_q));  // open: D, en, clk, clr
  Register #(.width(16)) register_5 (.Q(register_5_q));  // open: D, en, clk, clr
  Register #(.width(16)) register_6 (.Q(register_6_q));  // open: D, en, clk, clr
  FPMultiplier #(.fpwidth(16)) fpmultiplier_1 (.a(register_1_q), .b(inttofp_1_p2), .out(fpmultiplier_1_out));
  FPMultiplier #(.fpwidth(16)) fpmultiplier_2 (.a(register_2_q), .b(inttofp_1_p2), .out(inttofp_1_p3));
  FPMultiplier #(.fpwidth(16)) fpmultiplier_3 (.a(register_3_q), .b(inttofp_1_p2), .out(fpmultiplier_3_out));
  FPMultiplier #(.fpwidth(16)) fpmultiplier_4 (.a(register_4_q), .b(inttofp_1_p2), .out(fpmultiplier_4_out));
  FPMultiplier #(.fpwidth(16)) fpmultiplier_5 (.a(register_5_q), .b(inttofp_1_p2), .out(fpmultiplier_5_out));
  FPMultiplier #(.fpwidth(16)) fpmultiplier_6 (.a(register_6_q), .b(inttofp_1_p2), .out(fpmultiplier_6_out));
  FPDivider #(.fpwidth(16)) fpdivider_1 (.a(fpsubtractor_2_out), .b(fpsubtractor_1_out), .out(fpdivider_1_out));
  FPSubtractor #(.fpwidth(16)) fpsubtractor_1 (
    .a(fpmultiplier_1_out), .b(fpmultiplier_3_out), .out(fpsubtractor_1_out));
  FPSubtractor #(.fpwidth(16)) fpsubtractor_2 (.a(inttofp_1_p3), .b(fpmultiplier_4_out), .out(fpsubtractor_2_out));
  FPDivider #(.fpwidth(16)) fpdivider_2 (.a(fpsubtractor_4_out), .b(fpsubtractor_3_out), .out(fpdivider_2_out));
  FPSubtractor #(.fpwidth(16)) fpsubtractor_3 (
    .a(fpmultiplier_3_out), .b(fpmultiplier_5_out), .out(fpsubtractor_3_out));
  FPSubtractor #(.fpwidth(16)) fpsubtractor_4 (
    .a(fpmultiplier_4_out), .b(fpmultiplier_6_out), .out(fpsubtractor_4_out));
  FPDivider #(.fpwidth(16)) fpdivider_3 (.a(fpsubtractor_6_out), .b(fpsubtractor_5_out), .out(fpdivider_3_out));
  FPSubtractor #(.fpwidth(16)) fpsubtractor_5 (
    .a(fpmultiplier_1_out), .b(fpmultiplier_5_out), .out(fpsubtractor_5_out));
  FPSubtractor #(.fpwidth(16)) fpsubtractor_6 (.a(inttofp_1_p3), .b(fpmultiplier_6_out), .out(fpsubtractor_6_out));
  FPMultiplier #(.fpwidth(16)) fpmultiplier_7 (.a(fpmultiplier_1_out), .b(fpdivider_1_out), .out(fpmultiplier_7_out));
  FPMultiplier #(.fpwidth(16)) fpmultiplier_8 (.a(fpmultiplier_1_out), .b(fpdivider_2_out), .out(fpmultiplier_8_out));
  FPSubtractor #(.fpwidth(16)) fpsubtractor_7 (
    .a(fpmultiplier_6_out), .b(fpmultiplier_9_out), .out(fpsubtractor_7_out));
  FPMultiplier #(.fpwidth(16)) fpmultiplier_9 (.a(fpmultiplier_5_out), .b(fpdivider_3_out), .out(fpmultiplier_9_out));
  FPSubtractor #(.fpwidth(16)) fpsubtractor_8 (.a(inttofp_1_p3), .b(fpmultiplier_7_out), .out(fpsubtractor_8_out));
  FPSubtractor #(.fpwidth(16)) fpsubtractor_9 (.a(inttofp_1_p3), .b(fpmultiplier_8_out), .out(fpsubtractor_9_out));
  FPSubtractor #(.fpwidth(16)) fpsubtractor_10 (.a(fpsubtractor_8_out), .b(inttofp_1_p3), .out(fpsubtractor_10_out));
  FPSubtractor #(.fpwidth(16)) fpsubtractor_11 (
    .a(fpsubtractor_9_out), .b(fpmultiplier_4_out), .out(fpsubtractor_11_out));
  FPSubtractor #(.fpwidth(16)) fpsubtractor_12 (
    .a(fpsubtractor_7_out), .b(fpmultiplier_6_out), .out(fpsubtractor_12_out));
  FPDivider #(.fpwidth(16)) fpdivider_4 (.a(fpsubtractor_10_out), .b(fpdivider_1_out));  // open: out
  FPDivider #(.fpwidth(16)) fpdivider_5 (.a(fpsubtractor_11_out), .b(fpdivider_2_out));  // open: out
  FPDivider #(.fpwidth(16)) fpdivider_6 (.a(fpsubtractor_12_out), .b(fpdivider_3_out));  // open: out
  // FPToInt #(.fpwidth(16)) fptoint_1: pin names not known; wires that end beside it: inttofp_1_p3, fptoint_1_p2
  // FPToInt #(.fpwidth(16)) fptoint_2: pin names not known; wires that end beside it: fpmultiplier_4_out, fptoint_2_p2
  // FPToInt #(.fpwidth(16)) fptoint_3: pin names not known; wires that end beside it: fpmultiplier_6_out, fptoint_3_p2
  // FPToInt #(.fpwidth(16)) fptoint_4: pin names not known; wires that end beside it: fptoint_4_p1
  // FPToInt #(.fpwidth(16)) fptoint_5: pin names not known; wires that end beside it: fptoint_5_p1
  // FPToInt #(.fpwidth(16)) fptoint_6: pin names not known; wires that end beside it: fptoint_6_p1, fptoint_6_p2
  Counter #(.ongoal("stay")) counter_1 (.D(fptoint_1_p2), .Q(counter_1_q));  // open: load, count, carry, up, clk, clr
  Multiplexer #(.width(8)) multiplexer_1 (
    .in0(fptoint_2_p2), .in1(fptoint_3_p2), .out(multiplexer_1_out), .sel(d_ff_1_q));
  Multiplexer #(.width(8)) multiplexer_2 (
    .in0(fptoint_4_p1), .in1(fptoint_5_p1), .out(multiplexer_2_out));  // open: sel
  Multiplexer #(.width(8)) multiplexer_3 (
    .in0(multiplexer_2_out), .in1(multiplexer_4_out), .out(multiplexer_3_out));  // open: sel
  Multiplexer #(.width(8)) multiplexer_4 (
    .in0(fptoint_4_p1), .in1(fptoint_6_p1), .out(multiplexer_4_out));  // open: sel
  Multiplexer #(.width(8)) multiplexer_5 (.in1(fptoint_6_p2), .out(multiplexer_5_out));  // open: in0, sel
  Multiplexer #(.width(8)) multiplexer_6 (
    .in0(multiplexer_5_out), .in1(multiplexer_7_out), .out(multiplexer_6_out));  // open: sel
  Multiplexer #(.width(8)) multiplexer_7 (.out(multiplexer_7_out));  // open: in0, in1, sel
  Multiplexer #(.width(8)) multiplexer_8 ();  // open: in0, in1, out, sel
  Comparator comparator_1 (.a(counter_1_q), .b(multiplexer_1_out), .gt(comparator_1_gt));  // open: eq, lt
  D_Flip_Flop d_ff_1 (.D(comparator_1_gt), .Q(d_ff_1_q));  // open: clk, Qn, preset, reset
  Counter #(.ongoal("stay")) xLeft (.D(multiplexer_3_out), .Q(xLeft_q));  // open: load, count, carry, up, clk, clr
  Register xRight (.D(multiplexer_6_out));  // open: en, Q, clk, clr
  // RGB_Video #(.height(256), .width(256)) rgb_video_1: pin names not known; wires that end beside it: xLeft_q, counter_1_q
endmodule
