// Logisim project v5.circ as structural Verilog: 23 circuits, main circuit main
module main (
);

  wire clock_1_out, clock_2_out, clock_3_out, clock_4_out, comparator_1_eq, comparator_2_eq, comparator_3_eq,
       comparator_4_eq, comparator_5_eq, comparator_7_lt, comparator_8_gt, Continue_out, cpu_1_write_enable,
       floatarithmetic_1_read_avail, floattostring_1_read_avail, gpu_1_clearscreen, gpu_1_writeenable,
       pausebreakpoint_1_pause, priority_encoder_1_p3, priority_encoder_1_p4, priority_encoder_1_p5,
       stringtofloat_1_write_enable;
  wire [3:0] priority_encoder_1_p1;
  wire [6:0] keyboard_1_data;
  wire [7:0] cpu_1_data_out, floatarithmetic_1_data_out, floattostring_1_data_out, gpu_1_current_command,
       gpu_1_xcoordinate, gpu_1_ycoordinate, multiplexer_1_out, numtostring_1_data_out, ram_1_dout,
       stringtofloat_1_out_3, stringtonum_1_data_out;
  wire [7:7] undriven;
  wire [15:0] cpu_1_address;
  wire [23:0] gpu_1_color;

  Button Continue (.out(Continue_out));
  LED Paused (.in(pausebreakpoint_1_pause));
  // Probe on cpu_1_address
  CPU cpu_1 (
    .DATA_IN(multiplexer_1_out), .Pause(pausebreakpoint_1_pause), .WRITE_ENABLE(cpu_1_write_enable),
    .DATA_OUT(cpu_1_data_out), .ADDRESS(cpu_1_address));
  RAM #(.addrWidth(16), .enables("line")) ram_1 (
    .addr(cpu_1_address), .we(cpu_1_write_enable), .clk(clock_1_out), .din(cpu_1_data_out), .dout(ram_1_dout));
  Clock clock_1 (.out(clock_1_out));
  // Probe on cpu_1_data_out
  // Probe on multiplexer_1_out
  PauseBreakpoint pausebreakpoint_1 (.Address(cpu_1_address), .Continue(Continue_out), .Pause(pausebreakpoint_1_pause));
  NumToString numtostring_1 (
    .DATA_IN(cpu_1_data_out), .Address(cpu_1_address), .DATA_OUT(numtostring_1_data_out));  // open: CHARS_REMAINING
  StringToNum stringtonum_1 (.DATA_IN(cpu_1_data_out), .ADDRESS(cpu_1_address), .DATA_OUT(stringtonum_1_data_out));
  GPU gpu_1 (
    .Address(cpu_1_address), .DATA_IN(cpu_1_data_out), .ClearScreen(gpu_1_clearscreen),
    .WriteEnable(gpu_1_writeenable), .XCoordinate(gpu_1_xcoordinate), .YCoordinate(gpu_1_ycoordinate),
    .CURRENT_COMMAND(gpu_1_current_command), .Color(gpu_1_color));  // open: Reset
  Multiplexer #(.select(4), .width(8)) multiplexer_1 (
    .in0(ram_1_dout), .in1({undriven[7], keyboard_1_data}), .in2(numtostring_1_data_out),
    .in3(stringtonum_1_data_out), .in4(stringtofloat_1_out_3), .in5(floattostring_1_data_out),
    .in6(floatarithmetic_1_data_out), .in7(gpu_1_current_command), .out(multiplexer_1_out),
    .sel(priority_encoder_1_p1));  // open: in8, in9, in10, in11, in12, in13, in14, in15
  // Probe on priority_encoder_1_p1
  StringToFloat stringtofloat_1 (
    .DATA_IN(cpu_1_data_out), .Address(cpu_1_address), .out_3(stringtofloat_1_out_3),
    .WRITE_ENABLE(stringtofloat_1_write_enable));
  Comparator #(.mode("unsigned"), .width(16)) comparator_1 (
    .a(cpu_1_address), .b(16'hff41), .eq(comparator_1_eq));  // open: gt, lt
  FloatToString floattostring_1 (
    .DATA_IN(cpu_1_data_out), .Address(cpu_1_address), .DATA_OUT(floattostring_1_data_out),
    .READ_AVAIL(floattostring_1_read_avail));
  FloatArithmetic floatarithmetic_1 (
    .DATA_IN(cpu_1_data_out), .Address(cpu_1_address), .DATA_OUT(floatarithmetic_1_data_out),
    .READ_AVAIL(floatarithmetic_1_read_avail));
  // Probe on floatarithmetic_1_data_out
  // Priority_Encoder #(.select(4)) priority_encoder_1: pin names not known; wires that end beside it: priority_encoder_1_p1, 1'b1, priority_encoder_1_p3, priority_encoder_1_p4, priority_encoder_1_p5, stringtofloat_1_write_enable, floattostring_1_read_avail, floatarithmetic_1_read_avail, comparator_1_eq
  Comparator #(.mode("unsigned"), .width(16)) comparator_2 (
    .a(cpu_1_address), .b(16'hff1d), .eq(comparator_2_eq));  // open: gt, lt
  Comparator #(.mode("unsigned"), .width(16)) comparator_3 (
    .a(cpu_1_address), .b(16'hff1e), .eq(comparator_3_eq));  // open: gt, lt
  Clock clock_2 (.out(clock_2_out));
  TTY #(.cols(64), .rows(24)) tty_1 (
    .data(cpu_1_data_out[6:0]), .clk(clock_2_out), .we(comparator_4_eq), .clr(comparator_5_eq));
  Comparator #(.width(16)) comparator_4 (.a(cpu_1_address), .b(16'hff02), .eq(comparator_4_eq));  // open: gt, lt
  Comparator #(.width(16)) comparator_5 (.a(cpu_1_address), .b(16'hff03), .eq(comparator_5_eq));  // open: gt, lt
  Comparator #(.width(16)) comparator_6 (.a(cpu_1_address), .b(16'hff04), .eq(priority_encoder_1_p3));  // open: gt, lt
  Comparator #(.mode("unsigned"), .width(16)) comparator_7 (
    .a(cpu_1_address), .b(16'hff1a), .lt(comparator_7_lt));  // open: gt, eq
  and and_1 (priority_encoder_1_p4, comparator_7_lt, comparator_8_gt);
  Comparator #(.mode("unsigned"), .width(16)) comparator_8 (
    .a(cpu_1_address), .b(16'hff11), .gt(comparator_8_gt));  // open: eq, lt
  or or_1 (priority_encoder_1_p5, comparator_2_eq, comparator_3_eq);
  Clock clock_3 (.out(clock_3_out));
  Keyboard #(.buflen(16)) keyboard_1 (
    .clk(clock_3_out), .re(priority_encoder_1_p3), .data(keyboard_1_data));  // open: clr, avail
  Clock clock_4 (.out(clock_4_out));
  // RGB_Video #(.cursor("No Cursor"), .height(256), .width(256)) rgb_video_1: pin names not known; wires that end beside it: gpu_1_clearscreen, clock_4_out, gpu_1_writeenable, gpu_1_xcoordinate, gpu_1_ycoordinate, gpu_1_color
endmodule

module CPU (
  input  [7:0] DATA_IN,
  input  Pause,
  output WRITE_ENABLE,
  output [7:0] DATA_OUT,
  output [15:0] ADDRESS
);

  wire and_1_out, and_2_out, clock_1_out, comparator_1_eq, comparator_2_eq, decoder_1_out1, decoder_1_out2,
       decoder_1_out3, decoder_1_out4, decoder_1_out5, decoder_1_out6, decoder_1_out7, decoder_1_out8,
       decoder_1_out9, decoder_1_out10, decoder_1_out11, decoder_1_out12, decoder_1_out13, decoder_1_out14,
       decoder_1_out15, DOUBLE_EXEC, or_2_out, or_3_out, or_4_out, PC_INCREMENT, SINGLE_EXEC;
  wire [3:0] ADDR_SEL, ARG0_q, ARG0_q_2, ARG1_q, ARG1_q_2, DEST, Opcode_q, Opcode_q_2, SRC;
  wire [7:0] A_q, and_3_out, B_q, CMP_q, FLAGS, FLAGS_q, multiplexer_2_out, pull_resistor_1_node,
       pull_resistor_2_node, pull_resistor_3_node;
  wire [15:0] adder_1_out, adder_2_out, ALU_OUT, bit_extender_1_out, D_q, DATA_BUS, DEST_DATA, IDX_q,
       multiplexer_3_out, multiplexer_6_out, multiplexer_7_out, multiplexer_8_out, PC_q, SP_q;
  wire [15:1] pull_resistor_4_node;

  Decoder #(.enable("false"), .select(4)) decoder_1 (
    .out1(decoder_1_out1), .out2(decoder_1_out2), .out3(decoder_1_out3), .out4(decoder_1_out4),
    .out5(decoder_1_out5), .out6(decoder_1_out6), .out7(decoder_1_out7), .out8(decoder_1_out8),
    .out9(decoder_1_out9), .out10(decoder_1_out10), .out11(decoder_1_out11), .out12(decoder_1_out12),
    .out13(decoder_1_out13), .out14(decoder_1_out14), .out15(decoder_1_out15), .sel(DEST));  // open: out0
  or or_1 (WRITE_ENABLE, decoder_1_out1, decoder_1_out2, decoder_1_out3, decoder_1_out4);
  Multiplexer #(.width(8)) multiplexer_1 (.in0(DATA_BUS[15:8]), .in1(DATA_BUS[7:0]), .out(DATA_OUT), .sel(or_4_out));
  Multiplexer #(.width(8)) multiplexer_2 (
    .in0(DATA_BUS[7:0]), .in1(DATA_BUS[15:8]), .out(multiplexer_2_out), .sel(decoder_1_out7));
  // Probe on DATA_BUS
  or or_2 (or_2_out, decoder_1_out7, decoder_1_out5);
  or or_3 (or_3_out, decoder_1_out6, decoder_1_out7);
  and and_1 (and_1_out, decoder_1_out9, comparator_1_eq);
  Register A (.D(multiplexer_2_out), .en(or_2_out), .Q(A_q), .clk(and_2_out));  // open: clr
  Register B (.D(DATA_BUS[7:0]), .en(or_3_out), .Q(B_q), .clk(and_2_out));  // open: clr
  Register #(.width(16)) D (.D(DATA_BUS), .en(decoder_1_out8), .Q(D_q), .clk(and_2_out));  // open: clr
  Counter #(.max('hffff), .width(16)) PC (
    .load(and_1_out), .D(DATA_BUS), .count(PC_INCREMENT), .Q(PC_q), .clk(and_2_out));  // open: carry, up, clr
  Register #(.width(16)) SP (.D(DATA_BUS), .en(decoder_1_out10), .Q(SP_q), .clk(and_2_out));  // open: clr
  Register #(.width(16)) IDX (.D(DATA_BUS), .en(decoder_1_out11), .Q(IDX_q), .clk(and_2_out));  // open: clr
  Register CMP (.D(DATA_BUS[7:0]), .en(decoder_1_out12), .Q(CMP_q), .clk(and_2_out));  // open: clr
  Register u_FLAGS (.D(FLAGS), .en(comparator_2_eq), .Q(FLAGS_q), .clk(and_2_out));  // open: clr
  Register Opcode (.D(DATA_BUS[7:0]), .en(decoder_1_out13), .Q({Opcode_q_2, Opcode_q}), .clk(and_2_out));  // open: clr
  Register ARG0 (.D(DATA_BUS[7:0]), .en(decoder_1_out14), .Q({ARG0_q_2, ARG0_q}), .clk(and_2_out));  // open: clr
  Register ARG1 (.D(DATA_BUS[7:0]), .en(decoder_1_out15), .Q({ARG1_q_2, ARG1_q}), .clk(and_2_out));  // open: clr
  and and_2 (and_2_out, ~Pause, clock_1_out);  // AND_Gate
  Clock clock_1 (.out(clock_1_out));
  assign and_3_out = CMP_q & FLAGS_q;  // AND_Gate and_3, 8 bits wide
  Pull_Resistor pull_resistor_1 (.node(pull_resistor_1_node));
  Pull_Resistor pull_resistor_2 (.node(pull_resistor_2_node));
  // Probe on {A_q, B_q}
  Comparator comparator_1 (.a(CMP_q), .b(and_3_out), .eq(comparator_1_eq));  // open: gt, lt
  Comparator #(.width(4)) comparator_2 (.a(Opcode_q_2), .b(4'b1100), .eq(comparator_2_eq));  // open: gt, lt
  Pull_Resistor pull_resistor_3 (.node(pull_resistor_3_node));
  Multiplexer #(.width(16)) multiplexer_3 (
    .in0({pull_resistor_1_node, DATA_IN}), .in1({DEST_DATA[7:0], DATA_IN}), .out(multiplexer_3_out),
    .sel(or_4_out));
  // Probe on multiplexer_3_out
  Multiplexer #(.select(4), .width(16)) multiplexer_4 (
    .in0({16{1'b0}}), .in1(multiplexer_3_out), .in2(multiplexer_3_out), .in3(multiplexer_3_out),
    .in4(multiplexer_3_out), .in5({pull_resistor_2_node, A_q}), .in6({pull_resistor_2_node, B_q}),
    .in7({A_q, B_q}), .in8(D_q), .in9(PC_q), .in10(SP_q), .in11(IDX_q), .in12(ALU_OUT),
    .in14({pull_resistor_3_node, ARG0_q_2, ARG0_q}), .in15({ARG0_q_2, ARG0_q, ARG1_q_2, ARG1_q}),
    .out(DATA_BUS), .sel(SRC));  // open: in13
  Multiplexer #(.select(4), .width(16)) multiplexer_5 (
    .in0({16{1'b0}}), .in1(multiplexer_3_out), .in2(multiplexer_3_out), .in3(multiplexer_3_out),
    .in4(multiplexer_3_out), .in5({pull_resistor_2_node, A_q}), .in6({pull_resistor_2_node, B_q}),
    .in7({A_q, B_q}), .in8(D_q), .in9(PC_q), .in10(SP_q), .in11(IDX_q), .in12(ALU_OUT),
    .in14({pull_resistor_3_node, ARG0_q_2, ARG0_q}), .in15({ARG0_q_2, ARG0_q, ARG1_q_2, ARG1_q}),
    .out(DEST_DATA), .sel(DEST));  // open: in13
  Adder #(.width(16)) adder_1 (
    .a(IDX_q), .b({ARG0_q_2, ARG0_q, ARG1_q_2, ARG1_q}), .out(adder_1_out));  // open: cin, cout
  Multiplexer #(.select(4), .width(16)) multiplexer_6 (
    .in0(bit_extender_1_out), .in1(multiplexer_3_out), .in2(multiplexer_3_out), .in3(multiplexer_3_out),
    .in4(multiplexer_3_out), .in5({pull_resistor_2_node, A_q}), .in6({pull_resistor_2_node, B_q}),
    .in7({A_q, B_q}), .in8(D_q), .in9(PC_q), .in10(SP_q), .in11(IDX_q),
    .in14({pull_resistor_3_node, ARG0_q_2, ARG0_q}), .in15({ARG0_q_2, ARG0_q, ARG1_q_2, ARG1_q}),
    .out(multiplexer_6_out), .sel(ARG0_q_2));  // open: in12, in13
  Multiplexer #(.select(4), .width(16)) multiplexer_7 (
    .in0(bit_extender_1_out), .in1(multiplexer_3_out), .in2(multiplexer_3_out), .in3(multiplexer_3_out),
    .in4(multiplexer_3_out), .in5({pull_resistor_2_node, A_q}), .in6({pull_resistor_2_node, B_q}),
    .in7({A_q, B_q}), .in8(D_q), .in9(PC_q), .in10(SP_q), .in11(IDX_q),
    .in14({pull_resistor_3_node, ARG0_q_2, ARG0_q}), .in15({ARG0_q_2, ARG0_q, ARG1_q_2, ARG1_q}),
    .out(multiplexer_7_out), .sel(ARG0_q));  // open: in12, in13
  or or_4 (or_4_out, DOUBLE_EXEC, SINGLE_EXEC);
  Adder #(.width(16)) adder_2 (
    .a(SP_q), .b({ARG0_q_2, ARG0_q, ARG1_q_2, ARG1_q}), .out(adder_2_out));  // open: cin, cout
  Multiplexer #(.select(4), .width(16)) multiplexer_8 (
    .in0({16{1'b0}}), .in1(multiplexer_3_out), .in2(multiplexer_3_out), .in3(multiplexer_3_out),
    .in4(ALU_OUT), .in5({pull_resistor_2_node, A_q}), .in6({pull_resistor_2_node, B_q}), .in7({A_q, B_q}),
    .in8(D_q), .in9(PC_q), .in10(adder_2_out), .in11(adder_1_out), .in12(ALU_OUT),
    .in14({pull_resistor_3_node, ARG0_q_2, ARG0_q}), .in15({ARG0_q_2, ARG0_q, ARG1_q_2, ARG1_q}),
    .out(multiplexer_8_out), .sel(ADDR_SEL));  // open: in13
  assign bit_extender_1_out = {{12{1'b0}}, ARG1_q};  // Bit_Extender bit_extender_1
  Pipeline pipeline_1 (
    .CLCK(and_2_out), .Opcode({Opcode_q_2, Opcode_q}), .Pause(Pause), .DEST(DEST), .SRC(SRC),
    .ADDR_SEL(ADDR_SEL), .PC_INCREMENT(PC_INCREMENT), .DOUBLE_EXEC(DOUBLE_EXEC), .SINGLE_EXEC(SINGLE_EXEC));
  Pull_Resistor pull_resistor_4 (.node({pull_resistor_4_node, DOUBLE_EXEC}));
  Adder #(.width(16)) adder_3 (
    .a(multiplexer_8_out), .b({pull_resistor_4_node, DOUBLE_EXEC}), .out(ADDRESS));  // open: cin, cout
  ALU alu_1 (
    .ALU_TOP(multiplexer_6_out), .ALU_BOTTOM(multiplexer_7_out), .ALU_OP(ARG1_q_2), .ALU_OUT(ALU_OUT),
    .FLAGS(FLAGS));
endmodule

module Pipeline (
  input  CLCK,
  input  [7:0] Opcode,
  input  Pause,
  output [3:0] DEST,
  output [3:0] SRC,
  output [3:0] ADDR_SEL,
  output PC_INCREMENT,
  output DOUBLE_EXEC,
  output SINGLE_EXEC
);

  wire and_1_out, comparator_1_gt, comparator_2_lt, comparator_3_gt, comparator_4_gt, comparator_5_lt,
       comparator_7_eq, decoder_1_out0, decoder_1_out3, not_1_out;
  wire [2:0] counter_1_q, DEST_ARG_data, multiplexer_3_out, multiplexer_4_out, multiplexer_5_out, or_1_out,
       SRC_ARG_data;
  wire [3:0] multiplexer_1_out, multiplexer_2_out, rom_1_data;

  ROM #(.addrWidth(4), .dataWidth(3)) SRC_ARG (.addr(Opcode[7:4]), .data(SRC_ARG_data));
  ROM #(.addrWidth(4), .dataWidth(3)) DEST_ARG (.addr(Opcode[3:0]), .data(DEST_ARG_data));
  Comparator #(.mode("unsigned"), .width(4)) comparator_1 (
    .a(Opcode[7:4]), .b(Opcode[3:0]), .gt(comparator_1_gt));  // open: eq, lt
  Multiplexer #(.width(4)) multiplexer_1 (
    .in0(Opcode[3:0]), .in1(Opcode[7:4]), .out(multiplexer_1_out), .sel(comparator_1_gt));
  Multiplexer #(.width(4)) multiplexer_2 (
    .in0(Opcode[7:4]), .in1(Opcode[3:0]), .out(multiplexer_2_out), .sel(comparator_1_gt));
  Comparator #(.mode("unsigned"), .width(4)) comparator_2 (
    .a(multiplexer_1_out), .b(4'b1111), .lt(comparator_2_lt));  // open: gt, eq
  Comparator #(.mode("unsigned"), .width(4)) comparator_3 (
    .a(multiplexer_1_out), .b(4'b0110), .gt(comparator_3_gt));  // open: eq, lt
  Comparator #(.mode("unsigned"), .width(4)) comparator_4 (
    .a(4'b0101), .b(multiplexer_2_out), .gt(comparator_4_gt));  // open: eq, lt
  Comparator #(.mode("unsigned"), .width(4)) comparator_5 (
    .a(4'b0000), .b(multiplexer_2_out), .lt(comparator_5_lt));  // open: gt, eq
  ROM #(.addrWidth(4), .dataWidth(4)) rom_1 (.addr(multiplexer_2_out), .data(rom_1_data));
  assign or_1_out = SRC_ARG_data | DEST_ARG_data;  // OR_Gate or_1, 3 bits wide
  Multiplexer #(.width(3)) multiplexer_3 (.in0(3'b011), .in1(3'b100), .out(multiplexer_3_out), .sel(and_1_out));
  Decoder #(.enable("false"), .select(3)) decoder_1 (
    .out0(decoder_1_out0), .out3(decoder_1_out3), .sel(counter_1_q));  // open: out1, out2, out4, out5, out6, out7
  and and_1 (and_1_out, comparator_3_gt, comparator_2_lt, comparator_4_gt, comparator_5_lt);
  Multiplexer #(.select(3), .width(3)) multiplexer_4 (
    .in0(or_1_out), .in1(or_1_out), .in2(or_1_out), .in3(multiplexer_3_out), .in4(multiplexer_3_out),
    .out(multiplexer_4_out), .sel(counter_1_q));  // open: in5, in6, in7
  // OR_Gate or_2 has open pins: in0=decoder_1_out0, in1=decoder_1_out3, out=open
  Multiplexer #(.select(3), .width(3)) multiplexer_5 (
    .in0(3'b011), .in1(3'b011), .in2(3'b011), .in3(3'b000), .in4(3'b000), .out(multiplexer_5_out),
    .sel(counter_1_q));  // open: in5, in6, in7
  // Probe on multiplexer_5_out
  Counter #(.max('h4), .width(3)) counter_1 (
    .load(comparator_7_eq), .D(multiplexer_5_out), .Q(counter_1_q), .clk(not_1_out), .clr(Pause));  // open: count, carry, up
  not not_1 (not_1_out, CLCK);
  Comparator #(.mode("unsigned"), .width(3)) comparator_6 ();  // open: a, b, gt, eq, lt
  Comparator #(.mode("unsigned"), .width(3)) comparator_7 (
    .a(multiplexer_4_out), .b(counter_1_q), .eq(comparator_7_eq));  // open: gt, lt
  Multiplexer #(.select(3), .width(8)) multiplexer_6 (
    .in0(8'h4d), .in1(8'h4e), .in2(8'h4f), .in3(Opcode), .in4(Opcode), .out({SRC, DEST}), .sel(counter_1_q));  // open: in5, in6, in7
  Multiplexer #(.select(3), .width(4)) multiplexer_7 (
    .in0(4'b1001), .in1(4'b1001), .in2(4'b1001), .in3(rom_1_data), .in4(rom_1_data), .out(ADDR_SEL),
    .sel(counter_1_q));  // open: in5, in6, in7
  Comparator #(.mode("unsigned"), .width(3)) comparator_8 (
    .a(counter_1_q), .b(3'b011), .lt(PC_INCREMENT));  // open: gt, eq
  Comparator #(.mode("unsigned"), .width(3)) comparator_9 (
    .a(counter_1_q), .b(3'b100), .eq(DOUBLE_EXEC));  // open: gt, lt
  not not_2 (SINGLE_EXEC, and_1_out);

  // Notes on the sheet:
  //   contents of SRC_ARG (hex, n*v repeats v):
  //   0 4*2 7*0 2 0 1 2
  //   contents of DEST_ARG (hex, n*v repeats v):
  //   0 4*2
  //   contents of rom_1 (hex, n*v repeats v):
  //   0 f a b 4
endmodule

module ALU (
  input  [15:0] ALU_TOP,
  input  [15:0] ALU_BOTTOM,
  input  [3:0] ALU_OP,
  output [15:0] ALU_OUT,
  output [7:0] FLAGS
);

  wire adder_1_cout, pull_resistor_5_node, pull_resistor_6_node, subtractor_1_bout;
  wire [14:0] pull_resistor_1_node, pull_resistor_2_node, pull_resistor_3_node, pull_resistor_4_node;
  wire [15:0] adder_1_out, and_1_out, divider_1_out, divider_1_rem, divider_2_out, multiplier_1_out,
       multiplier_2_out, not_1_out, or_1_out, subtractor_1_out, xor_1_out;

  assign and_1_out = ALU_TOP & ALU_BOTTOM;  // AND_Gate and_1, 16 bits wide
  assign or_1_out = ALU_TOP | ALU_BOTTOM;  // OR_Gate or_1, 16 bits wide
  assign xor_1_out = ALU_TOP ^ ALU_BOTTOM;  // XOR_Gate xor_1, 16 bits wide
  Adder #(.width(16)) adder_1 (.a(ALU_TOP), .b(ALU_BOTTOM), .out(adder_1_out), .cout(adder_1_cout));  // open: cin
  Subtractor #(.width(16)) subtractor_1 (
    .a(ALU_TOP), .b(ALU_BOTTOM), .out(subtractor_1_out), .bout(subtractor_1_bout));  // open: bin
  Multiplier #(.width(16)) multiplier_1 (.a(ALU_TOP), .b(ALU_BOTTOM), .out(multiplier_1_out));  // open: cin, cout
  Multiplier #(.mode("twosComplement"), .width(16)) multiplier_2 (
    .a(ALU_TOP), .b(ALU_BOTTOM), .out(multiplier_2_out));  // open: cin, cout
  Divider #(.width(16)) divider_1 (
    .a(ALU_TOP), .b(ALU_BOTTOM), .out(divider_1_out), .rem(divider_1_rem));  // open: upper
  Divider #(.mode("twosComplement"), .width(16)) divider_2 (
    .a(ALU_TOP), .b(ALU_BOTTOM), .out(divider_2_out));  // open: upper, rem
  assign not_1_out = ~ALU_TOP;  // NOT_Gate not_1, 16 bits wide
  Comparator #(.width(16)) comparator_1 (.a(ALU_TOP), .b(ALU_BOTTOM), .gt(FLAGS[1]), .eq(FLAGS[0]), .lt(FLAGS[2]));
  or or_2 (FLAGS[7], FLAGS[1], FLAGS[0]);
  Pull_Resistor pull_resistor_1 (.node(pull_resistor_1_node));
  Pull_Resistor pull_resistor_2 (.node(pull_resistor_2_node));
  Pull_Resistor pull_resistor_3 (.node(pull_resistor_3_node));
  not not_2 (FLAGS[3], FLAGS[0]);
  or or_3 (FLAGS[6], FLAGS[0], FLAGS[2]);
  Pull_Resistor pull_resistor_4 (.node(pull_resistor_4_node));
  Pull_Resistor pull_resistor_5 (.node(pull_resistor_5_node));
  Pull_Resistor pull_resistor_6 (.node(pull_resistor_6_node));
  Multiplexer #(.select(4)) multiplexer_1 (
    .in0(pull_resistor_5_node), .in1(pull_resistor_5_node), .in2(pull_resistor_5_node), .in3(adder_1_cout),
    .in4(subtractor_1_bout), .in5(pull_resistor_6_node), .in6(pull_resistor_6_node),
    .in7(pull_resistor_6_node), .in8(pull_resistor_6_node), .in9(pull_resistor_6_node),
    .in10(pull_resistor_6_node), .in11(pull_resistor_6_node), .in12(pull_resistor_6_node),
    .in13(pull_resistor_6_node), .in14(pull_resistor_6_node), .in15(pull_resistor_6_node), .out(FLAGS[5]),
    .sel(ALU_OP));
  Multiplexer #(.select(4), .width(16)) multiplexer_2 (
    .in0(and_1_out), .in1(or_1_out), .in2(xor_1_out), .in3(adder_1_out), .in4(subtractor_1_out),
    .in5(multiplier_1_out), .in6(multiplier_2_out), .in7(divider_1_out), .in8(divider_2_out),
    .in9(divider_1_rem), .in10(not_1_out), .in11({pull_resistor_4_node, FLAGS[3]}),
    .in12({pull_resistor_1_node, FLAGS[0]}), .in13({pull_resistor_2_node, FLAGS[1]}),
    .in14({pull_resistor_3_node, FLAGS[2]}), .out(ALU_OUT), .sel(ALU_OP));  // open: in15
  Comparator #(.mode("unsigned"), .width(16)) comparator_2 (
    .a(ALU_OUT), .b({16{1'b0}}), .eq(FLAGS[4]));  // open: gt, lt
  Pull_Resistor pull_resistor_7 (.node(FLAGS[4]));
endmodule

module NumToString (
  input  [7:0] DATA_IN,
  input  [15:0] Address,
  output [7:0] DATA_OUT,
  output [2:0] CHARS_REMAINING
);

  wire and_1_out, and_2_out, and_3_out, and_4_out, clock_1_out, comparator_1_eq, comparator_2_eq,
       comparator_3_eq, comparator_4_eq, comparator_5_eq, comparator_6_eq, comparator_7_eq, comparator_8_eq,
       comparator_9_eq, comparator_10_eq, comparator_11_eq, comparator_12_eq, comparator_13_eq,
       comparator_14_eq, d_ff_1_q, decoder_1_out0, decoder_1_out1, decoder_1_out2;
  wire [2:0] priority_encoder_1_out, priority_encoder_2_out;
  wire [7:0] adder_1_out, adder_2_out, adder_3_out, adder_4_out, adder_5_out, BOTTOM_q, multiplexer_1_out,
       multiplexer_2_out, multiplexer_3_out, multiplexer_4_out, multiplexer_5_out, shift_register_1_out,
       shift_register_1_q0, shift_register_1_q1, shift_register_1_q2, shift_register_1_q3,
       shift_register_1_q4, shift_register_1_q5, shift_register_1_q6, TOP_q;
  wire [15:0] divider_1_out, divider_1_rem, divider_2_out, divider_2_rem, divider_3_out, divider_3_rem,
       divider_4_out, divider_4_rem, divider_5_rem;

  Decoder #(.select(4)) decoder_1 (
    .out0(decoder_1_out0), .out1(decoder_1_out1), .out2(decoder_1_out2), .sel(Address[3:0]),
    .en(comparator_1_eq));  // open: out3, out4, out5, out6, out7, out8, out9, out10, out11, out12, out13, out14, out15
  Comparator #(.width(12)) comparator_1 (.a(Address[15:4]), .b(12'hff1), .eq(comparator_1_eq));  // open: gt, lt
  Clock clock_1 (.out(clock_1_out));
  // Probe on {TOP_q, BOTTOM_q}
  Register TOP (.D(DATA_IN), .en(decoder_1_out0), .Q(TOP_q), .clk(clock_1_out));  // open: clr
  Register BOTTOM (.D(DATA_IN), .en(decoder_1_out1), .Q(BOTTOM_q), .clk(clock_1_out));  // open: clr
  Divider #(.width(16)) divider_1 (
    .a({TOP_q, BOTTOM_q}), .b(16'ha), .out(divider_1_out), .rem(divider_1_rem));  // open: upper
  Divider #(.width(16)) divider_2 (
    .a(divider_1_out), .b(16'ha), .out(divider_2_out), .rem(divider_2_rem));  // open: upper
  Adder adder_1 (.a(divider_1_rem[7:0]), .b(8'h30), .out(adder_1_out));  // open: cin, cout
  Divider #(.width(16)) divider_3 (
    .a(divider_2_out), .b(16'ha), .out(divider_3_out), .rem(divider_3_rem));  // open: upper
  Adder adder_2 (.a(divider_2_rem[7:0]), .b(8'h30), .out(adder_2_out));  // open: cin, cout
  Comparator comparator_2 (.a(adder_1_out), .b(8'h30), .eq(comparator_2_eq));  // open: gt, lt
  Multiplexer #(.select(3), .width(8)) multiplexer_1 (
    .in0(adder_1_out), .in1({8{1'b0}}), .in2({8{1'b0}}), .in3({8{1'b0}}), .in4({8{1'b0}}), .in5({8{1'b0}}),
    .in6({8{1'b0}}), .in7({8{1'b0}}), .out(multiplexer_1_out), .sel(priority_encoder_1_out));
  Adder adder_3 (.a(divider_3_rem[7:0]), .b(8'h30), .out(adder_3_out));  // open: cin, cout
  Comparator comparator_3 (.a(adder_2_out), .b(8'h30), .eq(comparator_3_eq));  // open: gt, lt
  Multiplexer #(.select(3), .width(8)) multiplexer_2 (
    .in0(adder_2_out), .in1(adder_1_out), .in2({8{1'b0}}), .in3({8{1'b0}}), .in4({8{1'b0}}), .in5({8{1'b0}}),
    .in6({8{1'b0}}), .in7({8{1'b0}}), .out(multiplexer_2_out), .sel(priority_encoder_1_out));
  Divider #(.width(16)) divider_4 (
    .a(divider_3_out), .b(16'ha), .out(divider_4_out), .rem(divider_4_rem));  // open: upper
  Adder adder_4 (.a(divider_4_rem[7:0]), .b(8'h30), .out(adder_4_out));  // open: cin, cout
  Comparator comparator_4 (.a(adder_3_out), .b(8'h30), .eq(comparator_4_eq));  // open: gt, lt
  Multiplexer #(.select(3), .width(8)) multiplexer_3 (
    .in0(adder_3_out), .in1(adder_2_out), .in2(adder_1_out), .in3({8{1'b0}}), .in4({8{1'b0}}),
    .in5({8{1'b0}}), .in6({8{1'b0}}), .in7({8{1'b0}}), .out(multiplexer_3_out), .sel(priority_encoder_1_out));
  D_Flip_Flop #(.trigger("falling")) d_ff_1 (
    .clk(clock_1_out), .D(decoder_1_out1), .Q(d_ff_1_q));  // open: Qn, preset, reset
  Divider #(.width(16)) divider_5 (.a(divider_4_out), .b(16'ha), .rem(divider_5_rem));  // open: out, upper
  Adder adder_5 (.a(divider_5_rem[7:0]), .b(8'h30), .out(adder_5_out));  // open: cin, cout
  Comparator comparator_5 (.a(adder_4_out), .b(8'h30), .eq(comparator_5_eq));  // open: gt, lt
  Multiplexer #(.select(3), .width(8)) multiplexer_4 (
    .in0(adder_4_out), .in1(adder_3_out), .in2(adder_2_out), .in3(adder_1_out), .in4({8{1'b0}}),
    .in5({8{1'b0}}), .in6({8{1'b0}}), .in7({8{1'b0}}), .out(multiplexer_4_out), .sel(priority_encoder_1_out));
  Shift_Register #(.trigger("falling"), .width(8)) shift_register_1 (
    .shift(decoder_1_out2), .clk(clock_1_out), .out(shift_register_1_out), .load(d_ff_1_q), .d0({8{1'b0}}),
    .q0(shift_register_1_q0), .d1({8{1'b0}}), .q1(shift_register_1_q1), .d2({8{1'b0}}),
    .q2(shift_register_1_q2), .d3(multiplexer_1_out), .q3(shift_register_1_q3), .d4(multiplexer_2_out),
    .q4(shift_register_1_q4), .d5(multiplexer_3_out), .q5(shift_register_1_q5), .d6(multiplexer_4_out),
    .q6(shift_register_1_q6), .d7(multiplexer_5_out));  // open: in, clr, q7
  Comparator comparator_6 (.a(adder_5_out), .b(8'h30), .eq(comparator_6_eq));  // open: gt, lt
  Multiplexer #(.select(3), .width(8)) multiplexer_5 (
    .in0(adder_5_out), .in1(adder_4_out), .in2(adder_3_out), .in3(adder_2_out), .in4(adder_1_out),
    .in5(adder_1_out), .in6({8{1'b0}}), .in7({8{1'b0}}), .out(multiplexer_5_out), .sel(priority_encoder_1_out));
  // Probe on shift_register_1_out
  // Probe on shift_register_1_q6
  // Probe on shift_register_1_q5
  // Probe on shift_register_1_q4
  // Probe on shift_register_1_q3
  and and_1 (and_1_out, comparator_6_eq, comparator_5_eq);
  and and_2 (and_2_out, and_1_out, comparator_4_eq);
  Comparator #(.mode("unsigned")) comparator_7 (
    .a(shift_register_1_out), .b({8{1'b0}}), .eq(comparator_7_eq));  // open: gt, lt
  Comparator #(.mode("unsigned")) comparator_8 (
    .a(shift_register_1_q6), .b({8{1'b0}}), .eq(comparator_8_eq));  // open: gt, lt
  Comparator #(.mode("unsigned")) comparator_9 (
    .a(shift_register_1_q5), .b({8{1'b0}}), .eq(comparator_9_eq));  // open: gt, lt
  Comparator #(.mode("unsigned")) comparator_10 (
    .a(shift_register_1_q4), .b({8{1'b0}}), .eq(comparator_10_eq));  // open: gt, lt
  Comparator #(.mode("unsigned")) comparator_11 (
    .a(shift_register_1_q3), .b({8{1'b0}}), .eq(comparator_11_eq));  // open: gt, lt
  Comparator #(.mode("unsigned")) comparator_12 (
    .a(shift_register_1_q2), .b({8{1'b0}}), .eq(comparator_12_eq));  // open: gt, lt
  Comparator #(.mode("unsigned")) comparator_13 (
    .a(shift_register_1_q1), .b({8{1'b0}}), .eq(comparator_13_eq));  // open: gt, lt
  Comparator #(.mode("unsigned")) comparator_14 (
    .a(shift_register_1_q0), .b({8{1'b0}}), .eq(comparator_14_eq));  // open: gt, lt
  and and_3 (and_3_out, and_2_out, comparator_3_eq);
  and and_4 (and_4_out, and_3_out, comparator_2_eq);
  Multiplexer #(.enable("true"), .select(4), .width(8)) multiplexer_6 (
    .in2(shift_register_1_out), .in3(shift_register_1_out), .in4(shift_register_1_out),
    .in5(shift_register_1_q6), .in6(shift_register_1_q5), .in7(shift_register_1_q4),
    .in8(shift_register_1_q3), .in9(shift_register_1_q2), .in10(shift_register_1_q1),
    .in11(shift_register_1_q0), .out(DATA_OUT), .sel(Address[3:0]), .en(comparator_1_eq));  // open: in0, in1, in12, in13, in14, in15
  Priority_Encoder priority_encoder_1 (
    .in0(1'b1), .in1(comparator_6_eq), .in2(and_1_out), .in3(and_2_out), .in4(and_3_out), .in5(and_4_out),
    .out(priority_encoder_1_out));  // open: in6, in7, en_in, gs, en_out
  Priority_Encoder priority_encoder_2 (
    .in0(comparator_14_eq), .in1(comparator_13_eq), .in2(comparator_12_eq), .in3(comparator_11_eq),
    .in4(comparator_10_eq), .in5(comparator_9_eq), .in6(comparator_8_eq), .in7(comparator_7_eq),
    .out(priority_encoder_2_out));  // open: en_in, gs, en_out
  Subtractor #(.width(3)) subtractor_1 (
    .a(3'b111), .b(priority_encoder_2_out), .out(CHARS_REMAINING));  // open: bin, bout
endmodule

module StringToNum (
  input  [7:0] DATA_IN,
  input  [15:0] ADDRESS,
  output [7:0] DATA_OUT
);

  wire and_1_out, clock_1_out, comparator_1_lt, comparator_2_gt, comparator_3_eq, comparator_4_eq,
       comparator_5_eq;
  wire [7:0] shift_register_1_out, shift_register_1_q0, shift_register_1_q1, shift_register_1_q2,
       shift_register_1_q3, subtractor_1_out;
  wire [15:0] adder_1_out, adder_2_out, adder_3_out, adder_4_out, multiplier_1_out, multiplier_2_out,
       multiplier_3_out, multiplier_4_out;
  wire [15:8] pull_resistor_1_node, pull_resistor_2_node, pull_resistor_3_node, pull_resistor_4_node,
       pull_resistor_5_node;

  Comparator #(.mode("unsigned")) comparator_1 (.a(DATA_IN), .b(8'h3a), .lt(comparator_1_lt));  // open: gt, eq
  Comparator #(.mode("unsigned")) comparator_2 (.a(DATA_IN), .b(8'h2f), .gt(comparator_2_gt));  // open: eq, lt
  Subtractor subtractor_1 (.a(DATA_IN), .b(8'h30), .out(subtractor_1_out));  // open: bin, bout
  Comparator #(.mode("unsigned"), .width(16)) comparator_3 (
    .a(ADDRESS), .b(16'hff1b), .eq(comparator_3_eq));  // open: gt, lt
  Comparator #(.mode("unsigned"), .width(16)) comparator_4 (
    .a(ADDRESS), .b(16'hff1c), .eq(comparator_4_eq));  // open: gt, lt
  and and_1 (and_1_out, comparator_1_lt, comparator_3_eq, comparator_2_gt);
  Clock clock_1 (.out(clock_1_out));
  Shift_Register #(.length(5), .width(8)) shift_register_1 (
    .shift(and_1_out), .in(subtractor_1_out), .clk(clock_1_out), .out(shift_register_1_out),
    .clr(comparator_4_eq), .q0(shift_register_1_q0), .q1(shift_register_1_q1), .q2(shift_register_1_q2),
    .q3(shift_register_1_q3));  // open: load, d0, d1, d2, d3, d4, q4
  Pull_Resistor pull_resistor_1 (.node({pull_resistor_1_node, shift_register_1_out}));
  Multiplier #(.width(16)) multiplier_1 (
    .a(16'h2710), .b({pull_resistor_1_node, shift_register_1_out}), .out(multiplier_1_out));  // open: cin, cout
  Pull_Resistor pull_resistor_2 (.node({pull_resistor_2_node, shift_register_1_q3}));
  Multiplier #(.width(16)) multiplier_2 (
    .a(16'h3e8), .b({pull_resistor_2_node, shift_register_1_q3}), .out(multiplier_2_out));  // open: cin, cout
  Pull_Resistor pull_resistor_3 (.node({pull_resistor_3_node, shift_register_1_q2}));
  Adder #(.width(16)) adder_1 (.a(multiplier_1_out), .b(multiplier_2_out), .out(adder_1_out));  // open: cin, cout
  Multiplier #(.width(16)) multiplier_3 (
    .a(16'h64), .b({pull_resistor_3_node, shift_register_1_q2}), .out(multiplier_3_out));  // open: cin, cout
  Pull_Resistor pull_resistor_4 (.node({pull_resistor_4_node, shift_register_1_q1}));
  Adder #(.width(16)) adder_2 (.a(adder_1_out), .b(multiplier_3_out), .out(adder_2_out));  // open: cin, cout
  Multiplier #(.width(16)) multiplier_4 (
    .a(16'ha), .b({pull_resistor_4_node, shift_register_1_q1}), .out(multiplier_4_out));  // open: cin, cout
  Pull_Resistor pull_resistor_5 (.node({pull_resistor_5_node, shift_register_1_q0}));
  Adder #(.width(16)) adder_3 (.a(adder_2_out), .b(multiplier_4_out), .out(adder_3_out));  // open: cin, cout
  Comparator #(.mode("unsigned"), .width(16)) comparator_5 (
    .a(ADDRESS), .b(16'hff1e), .eq(comparator_5_eq));  // open: gt, lt
  // Probe on adder_4_out
  Adder #(.width(16)) adder_4 (
    .a(adder_3_out), .b({pull_resistor_5_node, shift_register_1_q0}), .out(adder_4_out));  // open: cin, cout
  Multiplexer #(.width(8)) multiplexer_1 (
    .in0(adder_4_out[15:8]), .in1(adder_4_out[7:0]), .out(DATA_OUT), .sel(comparator_5_eq));
endmodule

module GPU (
  input  [15:0] Address,
  input  [7:0] DATA_IN,
  input  Reset,
  output ClearScreen,
  output WriteEnable,
  output [7:0] XCoordinate,
  output [7:0] YCoordinate,
  output [7:0] CURRENT_COMMAND,
  output [23:0] Color
);

  wire and_1_out, and_2_out, and_3_out, clock_1_out, comparator_1_gt, comparator_2_lt, comparator_3_eq,
       comparator_4_eq, comparator_5_eq, comparator_6_eq, d_ff_1_q, decoder_1_out1, decoder_1_out2,
       decoder_1_out3, decoder_1_out4, decoder_1_out5, decoder_1_out6, decoder_1_out7, decoder_1_out8,
       decoder_1_out9, decoder_1_out10, decoder_1_out11, decoder_1_out12, decoder_1_out13, decoder_2_out3,
       decoder_2_out4, decoder_2_out5, decoder_2_out6, decoder_2_out7, linerasterizer_1_out_enable,
       linerasterizer_1_reset, multiplexer_3_out, or_1_out, or_2_out, or_3_out, or_4_out, s_r_ff_2_q,
       s_r_ff_3_q, triangle3d_1_reset, triangle3d_1_write_enable;
  wire [7:0] BColor_q, counter_1_q, counter_2_q, GColor_q, linerasterizer_1_xcoord, linerasterizer_1_ycoord,
       multiplexer_1_out, multiplexer_2_out, RColor_q, register_1_q, register_2_q, register_3_q,
       triangle3d_1_x_out, triangle3d_1_y_out, Vec3x_q, Vec3y_q, Vecx_q, VecY_q, XCoord_q, YCoord_q;
  wire [23:0] triangle3d_1_rgb;
  wire [47:0] register_4_q, register_5_q, register_6_q, register_7_q, register_8_q, register_9_q;

  Comparator #(.mode("unsigned"), .width(16)) comparator_1 (
    .a(Address), .b(16'hff40), .gt(comparator_1_gt));  // open: eq, lt
  and and_1 (and_1_out, comparator_1_gt, comparator_2_lt);
  Comparator #(.mode("unsigned"), .width(16)) comparator_2 (
    .a(Address), .b(16'hff4f), .lt(comparator_2_lt));  // open: gt, eq
  Decoder #(.select(4)) decoder_1 (
    .out1(decoder_1_out1), .out2(decoder_1_out2), .out3(decoder_1_out3), .out4(decoder_1_out4),
    .out5(decoder_1_out5), .out6(decoder_1_out6), .out7(decoder_1_out7), .out8(decoder_1_out8),
    .out9(decoder_1_out9), .out10(decoder_1_out10), .out11(decoder_1_out11), .out12(decoder_1_out12),
    .out13(decoder_1_out13), .sel(Address[3:0]), .en(and_1_out));  // open: out0, out14, out15
  // Probe on DATA_IN
  Register Command (.D(DATA_IN), .en(decoder_1_out1), .Q(CURRENT_COMMAND), .clk(clock_1_out), .clr(or_1_out));
  Register XCoord (.D(DATA_IN), .en(decoder_1_out2), .Q(XCoord_q), .clk(clock_1_out), .clr(Reset));
  Register YCoord (.D(DATA_IN), .en(decoder_1_out3), .Q(YCoord_q), .clk(clock_1_out), .clr(Reset));
  Register Vecx (.D(DATA_IN), .en(decoder_1_out4), .Q(Vecx_q), .clk(clock_1_out), .clr(Reset));
  Register VecY (.D(DATA_IN), .en(decoder_1_out5), .Q(VecY_q), .clk(clock_1_out), .clr(Reset));
  Register RColor (.D(DATA_IN), .en(decoder_1_out6), .Q(RColor_q), .clk(clock_1_out), .clr(Reset));
  Register GColor (.D(DATA_IN), .en(decoder_1_out7), .Q(GColor_q), .clk(clock_1_out), .clr(Reset));
  Register BColor (.D(DATA_IN), .en(decoder_1_out8), .Q(BColor_q), .clk(clock_1_out), .clr(Reset));
  Register Vec3x (.D(DATA_IN), .en(decoder_1_out9), .Q(Vec3x_q), .clk(clock_1_out));  // open: clr
  Register Vec3y (.D(DATA_IN), .en(decoder_1_out10), .Q(Vec3y_q), .clk(clock_1_out));  // open: clr
  Register register_1 (.D(DATA_IN), .en(decoder_1_out11), .Q(register_1_q), .clk(clock_1_out));  // open: clr
  Register register_2 (.D(DATA_IN), .en(decoder_1_out12), .Q(register_2_q), .clk(clock_1_out));  // open: clr
  Register register_3 (.D(DATA_IN), .en(decoder_1_out13), .Q(register_3_q), .clk(clock_1_out));  // open: clr
  Clock clock_1 (.out(clock_1_out));
  Comparator comparator_3 (.a(CURRENT_COMMAND), .b(8'h1), .eq(comparator_3_eq));  // open: gt, lt
  or or_1 (or_1_out, ClearScreen, or_4_out, linerasterizer_1_reset, s_r_ff_2_q);
  Comparator comparator_4 (.a(CURRENT_COMMAND), .b(8'h2), .eq(comparator_4_eq));  // open: gt, lt
  or or_2 (or_2_out, s_r_ff_2_q, comparator_5_eq);
  Counter #(.ongoal("load")) counter_1 (
    .load(or_2_out), .D(XCoord_q), .count(s_r_ff_3_q), .Q(counter_1_q), .clk(clock_1_out), .clr(Reset));  // open: carry, up
  Counter #(.ongoal("stay")) counter_2 (
    .load(s_r_ff_2_q), .D(YCoord_q), .count(comparator_5_eq), .Q(counter_2_q), .clk(clock_1_out), .clr(Reset));  // open: carry, up
  S_R_Flip_Flop s_r_ff_1 (
    .S(comparator_3_eq), .clk(clock_1_out), .R(ClearScreen), .Q(ClearScreen));  // open: Qn, preset, reset
  S_R_Flip_Flop s_r_ff_2 (
    .S(comparator_4_eq), .clk(clock_1_out), .R(s_r_ff_2_q), .Q(s_r_ff_2_q));  // open: Qn, preset, reset
  Comparator #(.mode("unsigned")) comparator_5 (.a(counter_1_q), .b(Vecx_q), .eq(comparator_5_eq));  // open: gt, lt
  Comparator #(.mode("unsigned")) comparator_6 (.a(counter_2_q), .b(VecY_q), .eq(comparator_6_eq));  // open: gt, lt
  Decoder #(.enable("false"), .select(4)) decoder_2 (
    .out3(decoder_2_out3), .out4(decoder_2_out4), .out5(decoder_2_out5), .out6(decoder_2_out6),
    .out7(decoder_2_out7), .sel(CURRENT_COMMAND[3:0]));  // open: out0, out1, out2, out8, out9, out10, out11, out12, out13, out14, out15
  S_R_Flip_Flop s_r_ff_3 (.S(s_r_ff_2_q), .R(and_2_out), .clk(clock_1_out), .Q(s_r_ff_3_q));  // open: reset, Qn, preset
  and and_2 (and_2_out, comparator_5_eq, comparator_6_eq);
  or or_3 (or_3_out, decoder_2_out5, decoder_2_out6, decoder_2_out7);
  D_Flip_Flop d_ff_1 (.D(or_3_out), .clk(clock_1_out), .Q(d_ff_1_q));  // open: Qn, preset, reset
  LineRasterizer linerasterizer_1 (
    .x1(XCoord_q), .y1(YCoord_q), .x2(Vecx_q), .y2(VecY_q), .Start(decoder_2_out4),
    .yCoord(linerasterizer_1_ycoord), .xCoord(linerasterizer_1_xcoord),
    .OUT_ENABLE(linerasterizer_1_out_enable), .Reset(linerasterizer_1_reset));
  Register #(.width(48)) register_4 (
    .D({RColor_q, GColor_q, Vecx_q, VecY_q, XCoord_q, YCoord_q}), .en(decoder_2_out5), .Q(register_4_q),
    .clk(clock_1_out));  // open: clr
  Register #(.width(48)) register_5 (
    .D({register_2_q, register_3_q, Vec3y_q, register_1_q, BColor_q, Vec3x_q}), .en(decoder_2_out5),
    .Q(register_5_q), .clk(clock_1_out));  // open: clr
  Register #(.width(48)) register_6 (
    .D({RColor_q, GColor_q, Vecx_q, VecY_q, XCoord_q, YCoord_q}), .en(decoder_2_out6), .Q(register_6_q),
    .clk(clock_1_out));  // open: clr
  Register #(.width(48)) register_7 (
    .D({register_2_q, register_3_q, Vec3y_q, register_1_q, BColor_q, Vec3x_q}), .en(decoder_2_out6),
    .Q(register_7_q), .clk(clock_1_out));  // open: clr
  Register #(.width(48)) register_8 (
    .D({RColor_q, GColor_q, Vecx_q, VecY_q, XCoord_q, YCoord_q}), .en(decoder_2_out7), .Q(register_8_q),
    .clk(clock_1_out));  // open: clr
  Register #(.width(48)) register_9 (
    .D({register_2_q, register_3_q, Vec3y_q, register_1_q, BColor_q, Vec3x_q}), .en(decoder_2_out7),
    .Q(register_9_q), .clk(clock_1_out));  // open: clr
  or or_4 (or_4_out, and_3_out, triangle3d_1_reset);
  and and_3 (and_3_out, or_3_out, d_ff_1_q);
  Multiplexer #(.width(8)) multiplexer_1 (
    .in0(counter_1_q), .in1(linerasterizer_1_xcoord), .out(multiplexer_1_out),
    .sel(linerasterizer_1_out_enable));
  Multiplexer #(.width(8)) multiplexer_2 (
    .in0(counter_2_q), .in1(linerasterizer_1_ycoord), .out(multiplexer_2_out),
    .sel(linerasterizer_1_out_enable));
  Multiplexer multiplexer_3 (
    .in0(s_r_ff_3_q), .in1(linerasterizer_1_out_enable), .out(multiplexer_3_out),
    .sel(linerasterizer_1_out_enable));
  Multiplexer multiplexer_4 (
    .in0(multiplexer_3_out), .in1(triangle3d_1_write_enable), .out(WriteEnable), .sel(decoder_2_out3));
  Multiplexer #(.width(8)) multiplexer_5 (
    .in0(multiplexer_1_out), .in1(triangle3d_1_x_out), .out(XCoordinate), .sel(decoder_2_out3));
  Multiplexer #(.width(8)) multiplexer_6 (
    .in0(multiplexer_2_out), .in1(triangle3d_1_y_out), .out(YCoordinate), .sel(decoder_2_out3));
  Multiplexer #(.width(24)) multiplexer_7 (
    .in0({RColor_q, GColor_q, BColor_q}), .in1(triangle3d_1_rgb), .out(Color), .sel(decoder_2_out3));
  triangle3d triangle3d_1 (
    .Clear_Buffer(ClearScreen), .x1(register_4_q[15:0]), .y1(register_4_q[31:16]), .z1(register_4_q[47:32]),
    .r1(register_5_q[15:0]), .g1(register_5_q[31:16]), .b1(register_5_q[47:32]), .x2(register_6_q[15:0]),
    .y2(register_6_q[31:16]), .z2(register_6_q[47:32]), .r2(register_7_q[15:0]), .g2(register_7_q[31:16]),
    .b2(register_7_q[47:32]), .x3(register_8_q[15:0]), .y3(register_8_q[31:16]), .z3(register_8_q[47:32]),
    .r3(register_9_q[15:0]), .g3(register_9_q[31:16]), .b3(register_9_q[47:32]), .Start(decoder_2_out3),
    .Write_Enable(triangle3d_1_write_enable), .x_out(triangle3d_1_x_out), .y_out(triangle3d_1_y_out),
    .rgb(triangle3d_1_rgb), .RESET(triangle3d_1_reset));
endmodule

module TrianglerRasterizer (
  input  [15:0] x1,
  input  [15:0] y1,
  input  [15:0] z1,
  input  [15:0] c1,
  input  [15:0] x2,
  input  [15:0] y2,
  input  [15:0] z2,
  input  [15:0] c2,
  input  [15:0] x3,
  input  [15:0] y3,
  input  [15:0] z3,
  input  [15:0] c3,
  input  Start
);

  wire dotproduct_1_uporiented, undriven;
  wire [1:0] sortfloats_1_order, sortfloats_1_order_2, sortfloats_1_order_3;
  wire [15:0] Color_b, Color_m, ColorTop_b, ColorTop_m, fpadder_1_out, fpadder_2_out, lineeq_1_y, lineeq_2_y,
       lineeq_3_y, lineeq_4_y, lineeq_5_y, lineeq_6_y, multiplexer_4_out, multiplexer_7_out,
       projection_1_x2d, projection_1_y2d, projection_2_x2d, projection_2_y2d, projection_3_x2d,
       projection_3_y2d, register_1_q, register_2_q, slope_1_b, slope_1_m, sortfloats_1_bottom, undriven_2,
       Y_b, Y_m, YTOP_b, YTOP_m, Z_b, Z_m, ZTOP_b, ZTOP_m;
  wire [63:0] multiplexer_1_out, multiplexer_2_out, multiplexer_3_out, multiplexer_5_out, multiplexer_6_out;

  RAM #(.addrWidth(16), .clearpin("true"), .dataWidth(16)) ZBuffer ();  // open: addr, we, oe, clk, din, dout, clr
  Projection projection_1 (.X(x1), .Y(y1), .Z(z1), .X2d(projection_1_x2d), .Y2d(projection_1_y2d));
  Projection projection_2 (.X(x2), .Y(y2), .Z(z2), .X2d(projection_2_x2d), .Y2d(projection_2_y2d));
  Projection projection_3 (.X(x3), .Y(y3), .Z(z3), .X2d(projection_3_x2d), .Y2d(projection_3_y2d));
  Multiplexer #(.select(2), .width(64)) multiplexer_1 (
    .in0({c1, z1, projection_1_y2d, projection_1_x2d}), .in1({c2, z2, projection_2_y2d, projection_2_x2d}),
    .in2({c3, z3, projection_3_y2d, projection_3_x2d}), .out(multiplexer_1_out), .sel(sortfloats_1_order));  // open: in3
  Multiplexer #(.select(2), .width(64)) multiplexer_2 (
    .in0({c1, z1, projection_1_y2d, projection_1_x2d}), .in1({c2, z2, projection_2_y2d, projection_2_x2d}),
    .in2({c3, z3, projection_3_y2d, projection_3_x2d}), .out(multiplexer_2_out), .sel(sortfloats_1_order_2));  // open: in3
  Multiplexer #(.select(2), .width(64)) multiplexer_3 (
    .in0({c1, z1, projection_1_y2d, projection_1_x2d}), .in1({c2, z2, projection_2_y2d, projection_2_x2d}),
    .in2({c3, z3, projection_3_y2d, projection_3_x2d}), .out(multiplexer_3_out), .sel(sortfloats_1_order_3));  // open: in3
  SortFloats sortfloats_1 (
    .A(projection_1_x2d), .B(z2), .C(z3),
    .Order({sortfloats_1_order_3, sortfloats_1_order_2, sortfloats_1_order}), .Bottom(sortfloats_1_bottom));  // open: TopOriented, Switch, Middle, TOP
  Multiplexer #(.width(16)) multiplexer_4 (
    .in0(sortfloats_1_bottom), .in1(fpadder_1_out), .out(multiplexer_4_out), .sel(undriven));
  Register #(.width(16)) register_1 (.D(multiplexer_4_out), .Q(register_1_q));  // open: en, clk, clr
  DotProduct dotproduct_1 (
    .X1(multiplexer_1_out[15:0]), .Y1(multiplexer_1_out[31:16]), .X2(multiplexer_2_out[15:0]),
    .Y2(multiplexer_2_out[31:16]), .X3(multiplexer_3_out[15:0]), .Y3(multiplexer_3_out[31:16]),
    .UpOriented(dotproduct_1_uporiented));  // open: Product
  FPAdder #(.fpwidth(16)) fpadder_1 (.a(register_1_q), .b(16'h3c00), .out(fpadder_1_out));
  Counter #(.max('h3), .width(2)) counter_1 ();  // open: load, D, count, Q, carry, up, clk, clr
  Multiplexer #(.width(64)) multiplexer_5 (
    .in0(multiplexer_2_out), .in1(multiplexer_3_out), .out(multiplexer_5_out), .sel(dotproduct_1_uporiented));
  Multiplexer #(.width(64)) multiplexer_6 (
    .in0(multiplexer_3_out), .in1(multiplexer_2_out), .out(multiplexer_6_out), .sel(dotproduct_1_uporiented));
  Slope YTOP (
    .x1(multiplexer_5_out[15:0]), .y1(multiplexer_5_out[31:16]), .x2(undriven_2),
    .y2(multiplexer_1_out[31:16]), .b(YTOP_b), .m(YTOP_m));
  Slope ZTOP (
    .x1(multiplexer_5_out[15:0]), .y1(multiplexer_5_out[47:32]), .x2(undriven_2),
    .y2(multiplexer_1_out[47:32]), .b(ZTOP_b), .m(ZTOP_m));
  Slope ColorTop (
    .x1(multiplexer_5_out[15:0]), .y1(multiplexer_5_out[63:48]), .x2(undriven_2),
    .y2(multiplexer_1_out[63:48]), .b(ColorTop_b), .m(ColorTop_m));
  Slope Y (
    .x1(multiplexer_6_out[15:0]), .y1(multiplexer_6_out[31:16]), .x2(multiplexer_1_out[15:0]),
    .y2(multiplexer_1_out[31:16]), .b(Y_b), .m(Y_m));
  Slope Z (
    .x1(multiplexer_6_out[15:0]), .y1(multiplexer_6_out[47:32]), .x2(multiplexer_1_out[15:0]),
    .y2(multiplexer_1_out[47:32]), .b(Z_b), .m(Z_m));
  Slope Color (
    .x1(multiplexer_6_out[15:0]), .y1(multiplexer_6_out[63:48]), .x2(multiplexer_1_out[15:0]),
    .y2(multiplexer_1_out[63:48]), .b(Color_b), .m(Color_m));
  LineEq lineeq_1 (.x(register_1_q), .m(YTOP_m), .b(YTOP_b), .y(lineeq_1_y));
  LineEq lineeq_2 (.x(register_1_q), .m(ZTOP_m), .b(ZTOP_b), .y(lineeq_2_y));
  LineEq lineeq_3 (.x(register_1_q), .m(ColorTop_m), .b(ColorTop_b), .y(lineeq_3_y));
  LineEq lineeq_4 (.x(register_1_q), .m(Y_m), .b(Y_b), .y(lineeq_4_y));
  LineEq lineeq_5 (.x(register_1_q), .m(Z_m), .b(Z_b), .y(lineeq_5_y));
  LineEq lineeq_6 (.x(register_1_q), .m(Color_m), .b(Color_b), .y(lineeq_6_y));
  Multiplexer #(.width(16)) multiplexer_7 (
    .in0(lineeq_1_y), .in1(fpadder_2_out), .out(multiplexer_7_out));  // open: sel
  Register #(.width(16)) register_2 (.D(multiplexer_7_out), .Q(register_2_q));  // open: en, clk, clr
  Slope slope_1 (.x1(register_2_q), .y1(lineeq_2_y), .x2(lineeq_4_y), .y2(lineeq_5_y), .b(slope_1_b), .m(slope_1_m));
  Slope slope_2 (.x1(register_2_q), .y1(lineeq_3_y), .x2(lineeq_4_y), .y2(lineeq_6_y));  // open: b, m
  FPAdder #(.fpwidth(16)) fpadder_2 (.a(register_2_q), .b(16'h3c00), .out(fpadder_2_out));
  LineEq lineeq_7 ();  // open: x, m, b, y
endmodule

module SortBytes (
  input  [7:0] A,
  input  [7:0] B,
  input  [7:0] C,
  output [7:0] TOP
);

  wire and_1_out, and_2_out, and_3_out, comparator_1_gt, comparator_1_lt, comparator_2_eq, comparator_2_gt,
       comparator_2_lt, comparator_3_gt, comparator_3_lt, inttofp_1_p1, or_1_out;
  wire [1:0] priority_encoder_1_out;

  Comparator #(.mode("unsigned")) comparator_1 (.a(A), .b(B), .gt(comparator_1_gt), .lt(comparator_1_lt));  // open: eq
  Comparator #(.mode("unsigned")) comparator_2 (
    .a(B), .b(C), .gt(comparator_2_gt), .eq(comparator_2_eq), .lt(comparator_2_lt));
  Comparator #(.mode("unsigned")) comparator_3 (.a(A), .b(C), .gt(comparator_3_gt), .lt(comparator_3_lt));  // open: eq
  Priority_Encoder #(.select(2)) priority_encoder_1 (
    .in0(and_1_out), .in1(and_2_out), .in2(and_3_out), .out(priority_encoder_1_out));  // open: in3
  and and_1 (and_1_out, comparator_1_gt, comparator_3_gt);
  and and_2 (and_2_out, comparator_1_lt, comparator_2_gt);
  Multiplexer #(.select(2), .width(8)) multiplexer_1 (
    .in0(A), .in1(B), .in2(C), .out(TOP), .sel(priority_encoder_1_out));  // open: in3
  Pull_Resistor pull_resistor_1 (.node(priority_encoder_1_out));
  and and_3 (and_3_out, or_1_out, comparator_3_lt);
  or or_1 (or_1_out, comparator_2_eq, comparator_2_lt);
  // IntToFP #(.mode("unsigned")) inttofp_1: pin names not known; wires that end beside it: inttofp_1_p1, inttofp_1_p1
endmodule

module LineRasterizer (
  input  [7:0] x1,
  input  [7:0] y1,
  input  [7:0] x2,
  input  [7:0] y2,
  input  Start,
  output [7:0] yCoord,
  output [7:0] xCoord,
  output OUT_ENABLE,
  output Reset
);

  wire and_1_out, clock_1_out, comparator_1_eq, comparator_2_eq, comparator_2_gt, comparator_3_gt,
       comparator_4_eq, comparator_4_gt, comparator_5_eq, comparator_6_eq, comparator_6_gt, comparator_7_eq,
       comparator_7_gt, fpcomparator_1_p3, multiplexer_1_out, or_1_out, or_2_out;
  wire [7:0] counter_1_q, counter_2_q, fptoint_1_p2, fptoint_2_p2, max_1_higher, max_1_lower, max_2_higher,
       max_2_lower, multiplexer_3_out;
  wire [31:0] fpadder_1_out, fpdivider_1_out, fpdivider_2_out, fpmultiplier_1_out, fpmultiplier_2_out,
       fpsubtractor_1_out, fpsubtractor_2_out, fpsubtractor_3_out, fpsubtractor_4_out, inttofp_1_p2,
       inttofp_2_p2, inttofp_3_p2, inttofp_4_p2, inttofp_5_p2, inttofp_6_p2;

  Clock clock_1 (.out(clock_1_out));
  // IntToFP #(.mode("unsigned")) inttofp_1: pin names not known; wires that end beside it: x1, inttofp_1_p2
  // IntToFP #(.mode("unsigned")) inttofp_2: pin names not known; wires that end beside it: y1, inttofp_2_p2
  // IntToFP #(.mode("unsigned")) inttofp_3: pin names not known; wires that end beside it: x2, inttofp_3_p2
  // IntToFP #(.mode("unsigned")) inttofp_4: pin names not known; wires that end beside it: y2, inttofp_4_p2
  Comparator #(.mode("unsigned")) comparator_1 (.a(x1), .b(x2), .eq(comparator_1_eq));  // open: gt, lt
  Max max_1 (.A(x1), .B(x2), .Lower(max_1_lower), .Higher(max_1_higher));
  and and_1 (and_1_out, Start, ~OUT_ENABLE);  // AND_Gate
  S_R_Flip_Flop s_r_ff_1 (
    .S(Start), .clk(clock_1_out), .R(multiplexer_1_out), .Q(OUT_ENABLE));  // open: Qn, preset, reset
  FPSubtractor fpsubtractor_1 (.a(inttofp_4_p2), .b(inttofp_2_p2), .out(fpsubtractor_1_out));
  FPSubtractor fpsubtractor_2 (.a(inttofp_3_p2), .b(inttofp_1_p2), .out(fpsubtractor_2_out));
  Counter counter_1 (
    .load(and_1_out), .D(max_1_lower), .count(OUT_ENABLE), .Q(counter_1_q), .clk(clock_1_out));  // open: carry, up, clr
  Counter counter_2 (
    .load(and_1_out), .D(max_2_lower), .count(OUT_ENABLE), .Q(counter_2_q), .clk(clock_1_out));  // open: carry, up, clr
  Max max_2 (.A(y2), .B(y1), .Lower(max_2_lower), .Higher(max_2_higher));
  FPDivider fpdivider_1 (.a(fpsubtractor_1_out), .b(fpsubtractor_2_out), .out(fpdivider_1_out));
  // IntToFP #(.mode("unsigned")) inttofp_5: pin names not known; wires that end beside it: counter_1_q, inttofp_5_p2
  Comparator #(.mode("unsigned")) comparator_2 (
    .a(counter_1_q), .b({8{1'b1}}), .gt(comparator_2_gt), .eq(comparator_2_eq));  // open: lt
  Comparator #(.mode("unsigned")) comparator_3 (
    .a(counter_1_q), .b(max_1_higher), .gt(comparator_3_gt));  // open: eq, lt
  Multiplexer multiplexer_1 (.in0(or_1_out), .in1(or_2_out), .out(multiplexer_1_out), .sel(fpcomparator_1_p3));
  FPMultiplier fpmultiplier_1 (.a(fpdivider_1_out), .b(inttofp_1_p2), .out(fpmultiplier_1_out));
  or or_1 (or_1_out, comparator_3_gt, comparator_2_eq, comparator_2_gt, comparator_7_gt, comparator_7_eq);
  // IntToFP #(.mode("unsigned")) inttofp_6: pin names not known; wires that end beside it: counter_2_q, inttofp_6_p2
  Comparator #(.mode("unsigned")) comparator_4 (
    .a(counter_2_q), .b({8{1'b1}}), .gt(comparator_4_gt), .eq(comparator_4_eq));  // open: lt
  Comparator #(.mode("unsigned")) comparator_5 (
    .a(counter_2_q), .b(max_2_higher), .eq(comparator_5_eq));  // open: gt, lt
  // Probe on fpdivider_1_out
  FPSubtractor fpsubtractor_3 (.a(inttofp_2_p2), .b(fpmultiplier_1_out), .out(fpsubtractor_3_out));
  FPMultiplier fpmultiplier_2 (.a(fpdivider_1_out), .b(inttofp_5_p2), .out(fpmultiplier_2_out));
  FPSubtractor fpsubtractor_4 (.a(inttofp_6_p2), .b(fpsubtractor_3_out), .out(fpsubtractor_4_out));
  Counter counter_3 ();  // open: load, D, count, Q, carry, up, clk, clr
  FPDivider fpdivider_2 (.a(fpsubtractor_4_out), .b(fpdivider_1_out), .out(fpdivider_2_out));
  FPAdder fpadder_1 (.a(fpmultiplier_2_out), .b(fpsubtractor_3_out), .out(fpadder_1_out));
  // FPToInt fptoint_1: pin names not known; wires that end beside it: fpdivider_2_out, fptoint_1_p2
  // Probe on fpsubtractor_3_out
  // Probe on 32'h3f800000
  // FPToInt fptoint_2: pin names not known; wires that end beside it: fpadder_1_out, fptoint_2_p2
  and and_2 (Reset, OUT_ENABLE, multiplexer_1_out);
  Comparator #(.mode("unsigned")) comparator_6 (
    .a(fptoint_1_p2), .b({8{1'b1}}), .gt(comparator_6_gt), .eq(comparator_6_eq));  // open: lt
  or or_2 (or_2_out, comparator_5_eq, comparator_4_eq, comparator_4_gt, comparator_6_eq, comparator_6_gt);
  // FPComparator fpcomparator_1: pin names not known; wires that end beside it: fpdivider_1_out, 32'h3f800000, fpcomparator_1_p3
  Comparator #(.mode("unsigned")) comparator_7 (
    .a(fptoint_2_p2), .b({8{1'b1}}), .gt(comparator_7_gt), .eq(comparator_7_eq));  // open: lt
  Multiplexer #(.width(8)) multiplexer_2 (.in0(fptoint_2_p2), .in1(counter_2_q), .out(yCoord), .sel(fpcomparator_1_p3));
  Multiplexer #(.width(8)) multiplexer_3 (
    .in0(counter_1_q), .in1(fptoint_1_p2), .out(multiplexer_3_out), .sel(fpcomparator_1_p3));
  Multiplexer #(.width(8)) multiplexer_4 (.in0(multiplexer_3_out), .in1(x2), .out(xCoord), .sel(comparator_1_eq));
endmodule

module Max (
  input  [7:0] A,
  input  [7:0] B,
  output [7:0] Lower,
  output [7:0] Higher
);

  wire comparator_1_eq, comparator_1_gt, comparator_1_lt, or_1_out;

  Comparator #(.mode("unsigned")) comparator_1 (
    .a(A), .b(B), .gt(comparator_1_gt), .eq(comparator_1_eq), .lt(comparator_1_lt));
  or or_1 (or_1_out, comparator_1_gt, comparator_1_eq);
  Multiplexer #(.width(8)) multiplexer_1 (.in0(A), .in1(B), .out(Lower), .sel(or_1_out));
  Multiplexer #(.width(8)) multiplexer_2 (.in0(A), .in1(B), .out(Higher), .sel(comparator_1_lt));
endmodule

module StringToFloat (
  input  [7:0] DATA_IN,
  input  [15:0] Address,
  output [7:0] out_3,
  output WRITE_ENABLE
);

  wire and_1_out, and_2_out, clock_1_out, comparator_1_eq, comparator_2_eq, comparator_3_eq, comparator_4_eq,
       comparator_5_eq, comparator_6_eq, comparator_7_eq, or_2_out;
  wire [3:0] Length_q, Period_q;
  wire [7:0] pull_resistor_1_node, register_3_q;
  wire [15:0] fpdivider_1_out, fpnegator_1_p2, inttofp_1_p2, inttofp_2_p2, multiplexer_3_out;
  wire [31:0] adder_1_out, multiplexer_1_out, multiplexer_2_out, multiplier_1_out, multiplier_2_out,
       register_1_q, register_2_q;
  wire [31:8] pull_resistor_1_node_2;

  Multiplier #(.width(32)) multiplier_1 (.a(32'ha), .b(register_1_q), .out(multiplier_1_out));  // open: cin, cout
  Clock clock_1 (.out(clock_1_out));
  Multiplexer #(.width(32)) multiplexer_1 (
    .in0(multiplier_1_out), .in1(32'h1), .out(multiplexer_1_out), .sel(and_1_out));
  Register #(.width(32)) register_1 (
    .D(multiplexer_1_out), .en(and_2_out), .Q(register_1_q), .clk(clock_1_out));  // open: clr
  Comparator #(.mode("unsigned"), .width(16)) comparator_1 (
    .a(Address), .b(16'hff50), .eq(comparator_1_eq));  // open: gt, lt
  Comparator #(.mode("unsigned"), .width(16)) comparator_2 (
    .a(Address), .b(16'hff51), .eq(comparator_2_eq));  // open: gt, lt
  Comparator #(.mode("unsigned"), .width(16)) comparator_3 (
    .a(Address), .b(16'hff52), .eq(comparator_3_eq));  // open: gt, lt
  Comparator comparator_4 (.a(DATA_IN), .b(8'h2), .eq(comparator_4_eq));  // open: gt, lt
  or or_1 (WRITE_ENABLE, comparator_2_eq, comparator_3_eq);
  Pull_Resistor pull_resistor_1 (.node({pull_resistor_1_node_2, pull_resistor_1_node}));
  Subtractor subtractor_1 (.a(DATA_IN), .b(8'h30), .out(pull_resistor_1_node));  // open: bin, bout
  Comparator comparator_5 (.a(DATA_IN), .b(8'h2e), .eq(comparator_5_eq));  // open: gt, lt
  or or_2 (or_2_out, comparator_5_eq, comparator_6_eq);
  Comparator comparator_6 (.a(DATA_IN), .b(8'h2d), .eq(comparator_6_eq));  // open: gt, lt
  Counter #(.max('hf), .width(4)) Length (
    .count(and_2_out), .Q(Length_q), .clk(clock_1_out), .clr(and_1_out));  // open: load, D, carry, up
  and and_1 (and_1_out, comparator_4_eq, comparator_1_eq);
  Multiplier #(.width(32)) multiplier_2 (
    .a({pull_resistor_1_node_2, pull_resistor_1_node}), .b(register_1_q), .out(multiplier_2_out));  // open: cin, cout
  and and_2 (and_2_out, ~or_2_out, comparator_1_eq);  // AND_Gate
  Register #(.width(4)) Period (.D(Length_q), .en(comparator_5_eq), .Q(Period_q), .clk(clock_1_out), .clr(and_1_out));
  Register #(.width(32)) register_2 (
    .D(adder_1_out), .en(and_2_out), .Q(register_2_q), .clk(clock_1_out), .clr(and_1_out));
  Adder #(.width(32)) adder_1 (.a(multiplier_2_out), .b(register_2_q), .out(adder_1_out));  // open: cin, cout
  // Probe on adder_1_out
  // Probe on inttofp_1_p2
  // IntToFP #(.fpwidth(16), .width(32)) inttofp_1: pin names not known; wires that end beside it: register_2_q, inttofp_1_p2
  Multiplexer #(.select(4), .width(32)) multiplexer_2 (
    .in0(32'h1), .in1(32'ha), .in2(32'h64), .in3(32'h3e8), .in4(32'h2710), .in5(32'h186a0), .in6(32'hf4240),
    .in7(32'h989680), .in8(32'h5f5e100), .in9(32'h3b9aca00), .in10(32'h3b9aca00), .in11(32'h3b9aca00),
    .in12(32'h3b9aca00), .in13(32'h3b9aca00), .in14(32'h3b9aca00), .in15(32'h3b9aca00),
    .out(multiplexer_2_out), .sel(Period_q));
  Register register_3 (.D(DATA_IN), .en(comparator_1_eq), .Q(register_3_q), .clk(clock_1_out));  // open: clr
  FPDivider #(.fpwidth(16)) fpdivider_1 (.a(inttofp_1_p2), .b(inttofp_2_p2), .out(fpdivider_1_out));
  // IntToFP #(.fpwidth(16), .width(32)) inttofp_2: pin names not known; wires that end beside it: multiplexer_2_out, inttofp_2_p2
  Comparator comparator_7 (.a(register_3_q), .b(8'h2d), .eq(comparator_7_eq));  // open: gt, lt
  Multiplexer #(.width(16)) multiplexer_3 (
    .in0(fpdivider_1_out), .in1(fpnegator_1_p2), .out(multiplexer_3_out), .sel(comparator_7_eq));
  // FPNegator #(.fpwidth(16)) fpnegator_1: pin names not known; wires that end beside it: fpdivider_1_out, fpnegator_1_p2
  // Probe on multiplexer_3_out
  Multiplexer #(.width(8)) multiplexer_4 (
    .in0(multiplexer_3_out[7:0]), .in1(multiplexer_3_out[15:8]), .out(out_3), .sel(comparator_2_eq));
endmodule

module FloatToString (
  input  [7:0] DATA_IN,
  input  [15:0] Address,
  output [7:0] DATA_OUT,
  output READ_AVAIL
);

  wire and_1_out, and_2_out, clock_1_out, comparator_1_eq, comparator_2_eq, comparator_2_lt, comparator_3_gt,
       comparator_5_eq, counter_1_carry, d_ff_1_q, s_r_ff_1_q;
  wire [1:0] counter_1_q, multiplexer_4_out;
  wire [2:0] numtostring_1_chars_remaining, register_2_q;
  wire [7:0] bit_extender_1_out, BOTTOM_q, counter_2_q, multiplexer_2_out, numtostring_1_data_out,
       register_1_q, subtractor_1_out, TOP_q;
  wire [15:0] fpmultiplier_1_out, fptoint_1_p2, inttofp_1_p2, multiplexer_3_out, pull_resistor_1_node;
  wire [31:0] multiplexer_1_out;

  Comparator #(.mode("unsigned"), .width(16)) comparator_1 (
    .a(Address), .b(16'hff53), .eq(comparator_1_eq));  // open: gt, lt
  Comparator #(.mode("unsigned"), .width(16)) comparator_2 (
    .a(16'hff54), .b(Address), .eq(comparator_2_eq), .lt(comparator_2_lt));  // open: gt
  and and_1 (and_1_out, comparator_2_lt, comparator_3_gt);
  Comparator #(.mode("unsigned"), .width(16)) comparator_3 (
    .a(16'hff56), .b(Address), .gt(comparator_3_gt), .eq(READ_AVAIL));  // open: lt
  Clock clock_1 (.out(clock_1_out));
  Register TOP (.D(DATA_IN), .en(comparator_2_eq), .Q(TOP_q), .clk(clock_1_out));  // open: clr
  Register BOTTOM (.D(DATA_IN), .en(and_1_out), .Q(BOTTOM_q), .clk(clock_1_out));  // open: clr
  // Probe on {TOP_q, BOTTOM_q}
  FPMultiplier #(.fpwidth(16)) fpmultiplier_1 (.a(inttofp_1_p2), .b({TOP_q, BOTTOM_q}), .out(fpmultiplier_1_out));
  Register register_1 (.D(DATA_IN), .en(comparator_1_eq), .Q(register_1_q), .clk(clock_1_out));  // open: clr
  Multiplexer #(.select(4), .width(32)) multiplexer_1 (
    .in0(32'h1), .in1(32'ha), .in2(32'h64), .in3(32'h3e8), .in4(32'h2710), .in5(32'h186a0), .in6(32'hf4240),
    .in7(32'h989680), .in8(32'h5f5e100), .in9(32'h3b9aca00), .in10(32'h3b9aca00), .in11(32'h3b9aca00),
    .in12(32'h3b9aca00), .in13(32'h3b9aca00), .in14(32'h3b9aca00), .in15(32'h3b9aca00),
    .out(multiplexer_1_out), .sel(register_1_q[3:0]));
  // Probe on fptoint_1_p2
  // FPToInt #(.fpwidth(16), .width(16)) fptoint_1: pin names not known; wires that end beside it: fpmultiplier_1_out, fptoint_1_p2
  S_R_Flip_Flop s_r_ff_1 (
    .S(and_1_out), .clk(clock_1_out), .R(counter_1_carry), .Q(s_r_ff_1_q));  // open: Qn, preset, reset
  // IntToFP #(.fpwidth(16), .width(32)) inttofp_1: pin names not known; wires that end beside it: multiplexer_1_out, inttofp_1_p2
  Pull_Resistor pull_resistor_1 (.node(pull_resistor_1_node));
  Counter #(.max('h2), .width(2)) counter_1 (
    .load(and_1_out), .D(2'b01), .count(s_r_ff_1_q), .Q(counter_1_q), .carry(counter_1_carry),
    .clk(clock_1_out));  // open: up, clr
  and and_2 (and_2_out, ~comparator_5_eq, READ_AVAIL);  // AND_Gate
  // Probe on multiplexer_2_out
  Multiplexer #(.width(8)) multiplexer_2 (
    .in0(fptoint_1_p2[15:8]), .in1(fptoint_1_p2[7:0]), .out(multiplexer_2_out), .sel(multiplexer_3_out[0]));
  Multiplexer #(.select(2), .width(16)) multiplexer_3 (
    .in0(pull_resistor_1_node), .in1(16'hff10), .in2(16'hff11), .in3(16'hff12), .out(multiplexer_3_out),
    .sel(multiplexer_4_out));
  Multiplexer #(.width(2)) multiplexer_4 (.in0(counter_1_q), .in1(2'b11), .out(multiplexer_4_out), .sel(and_2_out));
  // Probe on multiplexer_3_out
  Counter #(.ongoal("stay")) counter_2 (
    .count(READ_AVAIL), .Q(counter_2_q), .clk(clock_1_out), .clr(comparator_1_eq));  // open: load, D, carry, up
  Comparator #(.mode("unsigned")) comparator_4 (.a(counter_2_q), .b({8{1'b0}}));  // open: gt, eq, lt
  D_Flip_Flop d_ff_1 (.clk(clock_1_out), .D(counter_1_carry), .Q(d_ff_1_q));  // open: Qn, preset, reset
  Subtractor subtractor_1 (.a(bit_extender_1_out), .b(register_1_q), .out(subtractor_1_out));  // open: bin, bout
  NumToString numtostring_1 (
    .DATA_IN(multiplexer_2_out), .Address(multiplexer_3_out), .DATA_OUT(numtostring_1_data_out),
    .CHARS_REMAINING(numtostring_1_chars_remaining));
  Multiplexer #(.width(8)) multiplexer_5 (
    .in0(numtostring_1_data_out), .in1(8'h2e), .out(DATA_OUT), .sel(comparator_5_eq));
  Comparator #(.mode("unsigned")) comparator_5 (
    .a(subtractor_1_out), .b(counter_2_q), .eq(comparator_5_eq));  // open: gt, lt
  Register #(.width(3)) register_2 (
    .D(numtostring_1_chars_remaining), .en(d_ff_1_q), .Q(register_2_q), .clk(clock_1_out));  // open: clr
  TTY #(.cols(16), .rows(1)) tty_1 (.data(DATA_OUT[6:0]), .clk(clock_1_out), .we(READ_AVAIL), .clr(comparator_1_eq));
  assign bit_extender_1_out = {{5{1'b0}}, register_2_q};  // Bit_Extender bit_extender_1
endmodule

module FloatArithmetic (
  input  [7:0] DATA_IN,
  input  [15:0] Address,
  output [7:0] DATA_OUT,
  output READ_AVAIL
);

  wire and_1_out, clock_1_out, comparator_1_gt, comparator_2_gt, comparator_3_gt, comparator_4_gt,
       decoder_1_out0, decoder_1_out1, decoder_1_out2, decoder_1_out3;
  wire [2:0] undriven;
  wire [7:0] bit_extender_1_out, fpadder_1_out, fpadder_1_out_2, fpdivider_1_out, fpdivider_1_out_2,
       fpmultiplier_1_out, fpmultiplier_1_out_2, fpnegator_1_p2, fpnegator_1_p2_2, fpsubtractor_1_out,
       fpsubtractor_1_out_2, fptoint_1_p2, fptoint_1_p2_2, inttofp_1_p2, inttofp_1_p2_2,
       pull_resistor_1_node, register_1_q, register_2_q, register_3_q, register_4_q;

  Decoder #(.select(4)) decoder_1 (
    .out0(decoder_1_out0), .out1(decoder_1_out1), .out2(decoder_1_out2), .out3(decoder_1_out3),
    .sel(Address[3:0]), .en(and_1_out));  // open: out4, out5, out6, out7, out8, out9, out10, out11, out12, out13, out14, out15
  Comparator #(.mode("unsigned"), .width(16)) comparator_1 (
    .a(Address), .b(16'hff59), .gt(comparator_1_gt));  // open: eq, lt
  and and_1 (and_1_out, comparator_1_gt, comparator_2_gt);
  Comparator #(.mode("unsigned"), .width(16)) comparator_2 (
    .a(16'hff70), .b(Address), .gt(comparator_2_gt));  // open: eq, lt
  Comparator #(.mode("unsigned"), .width(16)) comparator_3 (
    .a(Address), .b(16'hff69), .gt(comparator_3_gt));  // open: eq, lt
  and and_2 (READ_AVAIL, comparator_3_gt, comparator_4_gt);
  Comparator #(.mode("unsigned"), .width(16)) comparator_4 (
    .a(16'hff80), .b(Address), .gt(comparator_4_gt));  // open: eq, lt
  Clock clock_1 (.out(clock_1_out));
  Register register_1 (.D(DATA_IN), .en(decoder_1_out0), .Q(register_1_q), .clk(clock_1_out));  // open: clr
  Register register_2 (.D(DATA_IN), .en(decoder_1_out1), .Q(register_2_q), .clk(clock_1_out));  // open: clr
  Register register_3 (.D(DATA_IN), .en(decoder_1_out2), .Q(register_3_q), .clk(clock_1_out));  // open: clr
  Register register_4 (.D(DATA_IN), .en(decoder_1_out3), .Q(register_4_q), .clk(clock_1_out));  // open: clr
  // Probe on {register_3_q, register_4_q}
  // Probe on {register_1_q, register_2_q}
  // Probe on {fpdivider_1_out_2, fpdivider_1_out}
  // Probe on {fpadder_1_out_2, fpadder_1_out}
  // Probe on {fpadder_1_out_2, fpadder_1_out}
  FPAdder #(.fpwidth(16)) fpadder_1 (
    .a({register_1_q, register_2_q}), .b({register_3_q, register_4_q}), .out({fpadder_1_out_2, fpadder_1_out}));
  FPSubtractor #(.fpwidth(16)) fpsubtractor_1 (
    .a({register_1_q, register_2_q}), .b({register_3_q, register_4_q}),
    .out({fpsubtractor_1_out_2, fpsubtractor_1_out}));
  FPMultiplier #(.fpwidth(16)) fpmultiplier_1 (
    .a({register_1_q, register_2_q}), .b({register_3_q, register_4_q}),
    .out({fpmultiplier_1_out_2, fpmultiplier_1_out}));
  FPDivider #(.fpwidth(16)) fpdivider_1 (
    .a({register_1_q, register_2_q}), .b({register_3_q, register_4_q}),
    .out({fpdivider_1_out_2, fpdivider_1_out}));
  // FPNegator #(.fpwidth(16)) fpnegator_1: pin names not known; wires that end beside it: {register_1_q, register_2_q}, {fpnegator_1_p2_2, fpnegator_1_p2}
  // FPComparator #(.fpwidth(16)) fpcomparator_1: pin names not known; wires that end beside it: {register_1_q, register_2_q}, {register_3_q, register_4_q}
  // FPToInt #(.fpwidth(16), .mode("truncate"), .width(16)) fptoint_1: pin names not known; wires that end beside it: {register_1_q, register_2_q}, {fptoint_1_p2_2, fptoint_1_p2}
  // IntToFP #(.fpwidth(16), .width(16)) inttofp_1: pin names not known; wires that end beside it: {register_1_q, register_2_q}, {inttofp_1_p2_2, inttofp_1_p2}
  // Probe on {fpdivider_1_out_2, fpdivider_1_out}
  assign bit_extender_1_out = {{5{1'b0}}, undriven};  // Bit_Extender bit_extender_1
  Pull_Resistor pull_resistor_1 (.node(pull_resistor_1_node));
  // Probe on {fpmultiplier_1_out_2, fpmultiplier_1_out}
  Multiplexer #(.enable("true"), .select(4), .width(8)) multiplexer_1 (
    .in0(pull_resistor_1_node), .in1(bit_extender_1_out), .in2(fpadder_1_out_2), .in3(fpadder_1_out),
    .in4(fpsubtractor_1_out_2), .in5(fpsubtractor_1_out), .in6(fpmultiplier_1_out_2),
    .in7(fpmultiplier_1_out), .in8(fpdivider_1_out_2), .in9(fpdivider_1_out), .in10(fpnegator_1_p2_2),
    .in11(fpnegator_1_p2), .in12(fptoint_1_p2_2), .in13(fptoint_1_p2), .in14(inttofp_1_p2_2),
    .in15(inttofp_1_p2), .out(DATA_OUT), .sel(Address[3:0]), .en(READ_AVAIL));
endmodule

module PauseBreakpoint (
  input  [15:0] Address,
  input  Continue,
  output Pause
);

  wire clock_1_out, comparator_1_eq;

  Comparator #(.mode("unsigned"), .width(16)) comparator_1 (
    .a(Address), .b(16'hff06), .eq(comparator_1_eq));  // open: gt, lt
  Clock clock_1 (.out(clock_1_out));
  S_R_Flip_Flop s_r_ff_1 (.S(comparator_1_eq), .clk(clock_1_out), .R(Continue), .Q(Pause));  // open: Qn, preset, reset
endmodule

module Slope (
  input  [15:0] x1,
  input  [15:0] y1,
  input  [15:0] x2,
  input  [15:0] y2,
  output [15:0] m,
  output [15:0] b
);

  wire [15:0] fpmultiplier_1_out, fpsubtractor_1_out, fpsubtractor_2_out;

  // Probe on y1
  // Probe on x2
  // Probe on x1
  // Probe on y2
  FPSubtractor #(.fpwidth(16)) fpsubtractor_1 (.a(y2), .b(y1), .out(fpsubtractor_1_out));
  FPSubtractor #(.fpwidth(16)) fpsubtractor_2 (.a(x2), .b(x1), .out(fpsubtractor_2_out));
  FPDivider #(.fpwidth(16)) fpdivider_1 (.a(fpsubtractor_1_out), .b(fpsubtractor_2_out), .out(m));
  FPMultiplier #(.fpwidth(16)) fpmultiplier_1 (.a(m), .b(x1), .out(fpmultiplier_1_out));
  // Probe on m
  FPSubtractor #(.fpwidth(16)) fpsubtractor_3 (.a(y1), .b(fpmultiplier_1_out), .out(b));
  // Probe on b
endmodule

module SortFloats (
  input  [15:0] A,
  input  [15:0] B,
  input  [15:0] C,
  input  TopOriented,
  input  Switch,
  output [5:0] Order,
  output [15:0] TOP,
  output [15:0] Middle,
  output [15:0] Bottom
);

  wire and_1_out, and_2_out, and_3_out, and_4_out, and_5_out, and_6_out, fpcomparator_1_p3,
       fpcomparator_1_p4, fpcomparator_1_p5, fpcomparator_2_p3, fpcomparator_2_p4, fpcomparator_2_p5,
       fpcomparator_3_p3, fpcomparator_3_p4, or_1_out;
  wire [1:0] adder_1_out;

  // Probe on A
  // Probe on B
  // Probe on C
  // FPComparator #(.fpwidth(16)) fpcomparator_1: pin names not known; wires that end beside it: A, B, fpcomparator_1_p3, fpcomparator_1_p4, fpcomparator_1_p5, fpcomparator_1_p5
  // FPComparator #(.fpwidth(16)) fpcomparator_2: pin names not known; wires that end beside it: B, C, fpcomparator_2_p3, fpcomparator_2_p4, fpcomparator_2_p5
  // FPComparator #(.fpwidth(16)) fpcomparator_3: pin names not known; wires that end beside it: A, C, fpcomparator_3_p3, fpcomparator_3_p4
  Priority_Encoder #(.select(2)) priority_encoder_1 (
    .in0(and_1_out), .in1(and_2_out), .in2(and_4_out), .out(Order[1:0]));  // open: in3
  and and_1 (and_1_out, fpcomparator_1_p3, fpcomparator_3_p3);
  and and_2 (and_2_out, fpcomparator_1_p4, fpcomparator_2_p3);
  and and_3 (and_3_out, fpcomparator_1_p4, fpcomparator_3_p4);
  Multiplexer #(.select(2), .width(16)) multiplexer_1 (
    .in0(A), .in1(B), .in2(C), .out(TOP), .sel(Order[1:0]));  // open: in3
  and and_4 (and_4_out, or_1_out, fpcomparator_3_p4);
  or or_1 (or_1_out, fpcomparator_2_p4, fpcomparator_2_p5);
  and and_5 (and_5_out, fpcomparator_1_p3, or_1_out);
  and and_6 (and_6_out, fpcomparator_3_p3, fpcomparator_2_p3);
  // Priority_Encoder #(.select(2)) priority_encoder_2: pin names not known; wires that end beside it: and_3_out, and_5_out, Order[5:4], and_6_out
  Multiplexer #(.select(2), .width(16)) multiplexer_2 (
    .in0(A), .in1(B), .in2(C), .out(Bottom), .sel(Order[5:4]));  // open: in3
  Pull_Resistor pull_resistor_1 (.node(Order[1:0]));
  Pull_Resistor pull_resistor_2 (.node(Order[5:4]));
  // Probe on Bottom
  // Probe on TOP
  Adder #(.width(2)) adder_1 (.a(Order[1:0]), .b(Order[5:4]), .out(adder_1_out));  // open: cin, cout
  Subtractor #(.width(2)) subtractor_1 (.a(2'b11), .b(adder_1_out), .out(Order[3:2]));  // open: bin, bout
  Multiplexer #(.select(2), .width(16)) multiplexer_3 (
    .in0(A), .in1(B), .in2(C), .out(Middle), .sel(Order[3:2]));  // open: in3
  // Probe on Middle
endmodule

module Projection (
  input  [15:0] X,
  input  [15:0] Y,
  input  [15:0] Z,
  output [15:0] X2d,
  output [15:0] Y2d
);

  wire [15:0] fpadder_1_out, fpadder_2_out, fpdivider_1_out, fpmultiplier_1_out, fpmultiplier_2_out,
       fpmultiplier_3_out;

  // Probe on 16'h4000
  // Probe on X
  // Probe on Y
  // Probe on 16'h3c00
  FPMultiplier #(.fpwidth(16)) fpmultiplier_1 (.a(Z), .b(16'h4000), .out(fpmultiplier_1_out));
  FPMultiplier #(.fpwidth(16)) fpmultiplier_2 (.a(fpdivider_1_out), .b(X), .out(fpmultiplier_2_out));
  FPMultiplier #(.fpwidth(16)) fpmultiplier_3 (.a(Y), .b(fpdivider_1_out), .out(fpmultiplier_3_out));
  FPDivider #(.fpwidth(16)) fpdivider_1 (.a(16'h3c00), .b(fpmultiplier_1_out), .out(fpdivider_1_out));
  // Probe on 16'h3800
  FPAdder #(.fpwidth(16)) fpadder_1 (.a(fpmultiplier_2_out), .b(16'h3800), .out(fpadder_1_out));
  FPMultiplier #(.fpwidth(16)) fpmultiplier_4 (.a(fpadder_1_out), .b(16'h5bf8), .out(X2d));
  FPAdder #(.fpwidth(16)) fpadder_2 (.a(fpmultiplier_3_out), .b(16'h3800), .out(fpadder_2_out));
  FPMultiplier #(.fpwidth(16)) fpmultiplier_5 (.a(fpadder_2_out), .b(16'h5bf8), .out(Y2d));
  // Probe on 16'h5bf8
  // Probe on X2d
  // Probe on Y2d
endmodule

module DotProduct (
  input  [15:0] X1,
  input  [15:0] Y1,
  input  [15:0] X2,
  input  [15:0] Y2,
  input  [15:0] X3,
  input  [15:0] Y3,
  output [15:0] Product,
  output UpOriented
);

  wire [15:0] fpmultiplier_1_out, fpmultiplier_2_out, fpsubtractor_1_out, fpsubtractor_2_out,
       fpsubtractor_3_out, fpsubtractor_4_out;

  FPSubtractor #(.fpwidth(16)) fpsubtractor_1 (.a(X3), .b(X1), .out(fpsubtractor_1_out));
  FPMultiplier #(.fpwidth(16)) fpmultiplier_1 (
    .a(fpsubtractor_1_out), .b(fpsubtractor_2_out), .out(fpmultiplier_1_out));
  FPSubtractor #(.fpwidth(16)) fpsubtractor_2 (.a(Y2), .b(Y1), .out(fpsubtractor_2_out));
  FPSubtractor #(.fpwidth(16)) fpsubtractor_3 (.a(Y3), .b(Y1), .out(fpsubtractor_3_out));
  FPMultiplier #(.fpwidth(16)) fpmultiplier_2 (
    .a(fpsubtractor_3_out), .b(fpsubtractor_4_out), .out(fpmultiplier_2_out));
  FPSubtractor #(.fpwidth(16)) fpsubtractor_4 (.a(X2), .b(X1), .out(fpsubtractor_4_out));
  FPSubtractor #(.fpwidth(16)) fpsubtractor_5 (.a(fpmultiplier_1_out), .b(fpmultiplier_2_out), .out(Product));
  // FPComparator #(.fpwidth(16)) fpcomparator_1: pin names not known; wires that end beside it: Product, {16{1'b0}}, UpOriented
  // Probe on {16{1'b0}}
endmodule

module LineEq (
  input  [15:0] x,
  input  [15:0] m,
  input  [15:0] b,
  output [15:0] y
);

  wire [15:0] fpmultiplier_1_out;

  // Probe on x
  // Probe on m
  FPMultiplier #(.fpwidth(16)) fpmultiplier_1 (.a(x), .b(m), .out(fpmultiplier_1_out));
  // Probe on b
  // Probe on y
  FPAdder #(.fpwidth(16)) fpadder_1 (.a(fpmultiplier_1_out), .b(b), .out(y));
endmodule

module triangle3d (
  input  Clear_Buffer,
  input  [15:0] x1,
  input  [15:0] y1,
  input  [15:0] z1,
  input  [15:0] r1,
  input  [15:0] g1,
  input  [15:0] b1,
  input  [15:0] x2,
  input  [15:0] y2,
  input  [15:0] z2,
  input  [15:0] r2,
  input  [15:0] g2,
  input  [15:0] b2,
  input  [15:0] x3,
  input  [15:0] y3,
  input  [15:0] z3,
  input  [15:0] r3,
  input  [15:0] g3,
  input  [15:0] b3,
  input  Start,
  output Write_Enable,
  output [7:0] x_out,
  output [7:0] y_out,
  output [23:0] rgb,
  output RESET
);

  wire and_1_out, and_2_out, and_4_out, clock_1_out, counter_1_carry, dotproduct_1_uporiented,
       fpcomparator_1_p3, fpcomparator_1_p4, fpcomparator_4_p2, fpcomparator_5_p3, fpcomparator_6_p3,
       fpcomparator_7_p3, fpcomparator_7_p4, fpcomparator_8_p3, fpcomparator_9_p3, fpcomparator_10_p3,
       fpcomparator_11_p3, fpcomparator_12_p4, fptoint_3_p1, not_1_out, or_1_out, or_2_out, or_3_out,
       or_4_out, or_5_out, or_6_out, or_7_out;
  wire [1:0] sortfloats_1_order, sortfloats_1_order_2, sortfloats_1_order_3;
  wire [15:0] adder_1_out, BBOTTOM_b, BBOTTOM_m, bit_extender_1_out, bit_extender_2_out, BTOP_b, BTOP_m,
       fliptriangle_1_top_dest_color, fliptriangle_1_top_dest_color_2, fliptriangle_1_top_dest_color_3,
       fliptriangle_1_top_dest_pos_2, fliptriangle_1_top_src_color, fliptriangle_1_top_src_color_2,
       fliptriangle_1_top_src_color_3, fliptriangle_1_top_src_pos, fliptriangle_1_top_src_pos_2,
       fliptriangle_1_top_src_pos_3, fpadder_1_out, fpadder_2_out, fpcomparator_1_p2, fpmultiplier_1_out,
       fpmultiplier_2_out, fpmultiplier_3_out, GBOTTOM_b, GBOTTOM_m, GTOP_b, GTOP_m, lineeq_1_y, lineeq_2_y,
       lineeq_3_y, lineeq_4_y, lineeq_5_y, lineeq_6_y, lineeq_7_y, lineeq_8_y, lineeq_9_y, lineeq_10_y,
       lineeq_11_y, lineeq_12_y, lineeq_13_y, lineeq_14_y, maxfloat_1_lower, maxfloat_2_lower,
       maxfloat_3_lower, maxfloat_4_lower, maxfloat_5_higher, maxfloat_6_higher, maxfloat_7_higher,
       multiplexer_3_out, multiplexer_3_out_2, multiplexer_5_out, multiplexer_5_out_2, multiplexer_7_out,
       multiplexer_8_out, multiplier_1_out, RBOTTOM_b, RBOTTOM_m, register_2_q, RTOP_b, RTOP_m, slope_1_b,
       slope_1_m, slope_2_b, slope_2_m, slope_3_b, slope_3_m, slope_4_b, slope_4_m, sortfloats_1_bottom,
       sortfloats_1_middle, sortfloats_1_top, YBOTTOM_b, YBOTTOM_m, YTOP_b, YTOP_m, ZBOTTOM_b, ZBOTTOM_m,
       ZBuffer_dout, ZTOP_b, ZTOP_m;
  wire [31:0] fliptriangle_1_top_dest_pos, projection_1_x2d, projection_2_x2d, projection_3_x2d;
  wire [47:0] fliptriangle_1_bottom_dest_color, fliptriangle_1_bottom_dest_pos,
       fliptriangle_1_bottom_src_color, fliptriangle_1_bottom_src_pos, multiplexer_1_out, multiplexer_2_out,
       multiplexer_4_out, multiplexer_6_out;
  wire [47:32] multiplexer_3_out_3, multiplexer_5_out_3;

  // Probe on projection_2_x2d[15:0]
  // Probe on projection_2_x2d[31:16]
  // Probe on projection_3_x2d[15:0]
  // Probe on projection_3_x2d[31:16]
  // Probe on x1
  // Probe on y1
  // Probe on z1
  // Probe on projection_1_x2d[15:0]
  // Probe on projection_1_x2d[31:16]
  Projection projection_1 (.X(x1), .Y(y1), .Z(z1), .X2d(projection_1_x2d[15:0]), .Y2d(projection_1_x2d[31:16]));
  Projection projection_2 (.X(x2), .Y(y2), .Z(z2), .X2d(projection_2_x2d[15:0]), .Y2d(projection_2_x2d[31:16]));
  Projection projection_3 (.X(x3), .Y(y3), .Z(z3), .X2d(projection_3_x2d[15:0]), .Y2d(projection_3_x2d[31:16]));
  Clock clock_1 (.out(clock_1_out));
  SortFloats sortfloats_1 (
    .A(projection_1_x2d[15:0]), .B(projection_2_x2d[15:0]), .C(projection_3_x2d[15:0]),
    .Middle(sortfloats_1_middle), .Order({sortfloats_1_order_3, sortfloats_1_order_2, sortfloats_1_order}),
    .Bottom(sortfloats_1_bottom), .TOP(sortfloats_1_top));  // open: TopOriented, Switch
  // Probe on maxfloat_1_lower
  Multiplexer #(.select(2), .width(48)) multiplexer_1 (
    .in0({z1, projection_1_x2d}), .in1({z2, projection_2_x2d}), .in2({z3, projection_3_x2d}),
    .out(multiplexer_1_out), .sel(sortfloats_1_order_3));  // open: in3
  Multiplexer #(.select(2), .width(48)) multiplexer_2 (
    .in0({b1, g1, r1}), .in1({b2, g2, r2}), .in2({b3, g3, r3}), .out(multiplexer_2_out),
    .sel(sortfloats_1_order_3));  // open: in3
  Multiplexer #(.select(2), .width(48)) multiplexer_3 (
    .in0({z1, projection_1_x2d}), .in1({z2, projection_2_x2d}), .in2({z3, projection_3_x2d}),
    .out({multiplexer_3_out_3, multiplexer_3_out_2, multiplexer_3_out}), .sel(sortfloats_1_order_2));  // open: in3
  Multiplexer #(.select(2), .width(48)) multiplexer_4 (
    .in0({b1, g1, r1}), .in1({b2, g2, r2}), .in2({b3, g3, r3}), .out(multiplexer_4_out),
    .sel(sortfloats_1_order_2));  // open: in3
  Multiplexer #(.select(2), .width(48)) multiplexer_5 (
    .in0({z1, projection_1_x2d}), .in1({z2, projection_2_x2d}), .in2({z3, projection_3_x2d}),
    .out({multiplexer_5_out_3, multiplexer_5_out_2, multiplexer_5_out}), .sel(sortfloats_1_order));  // open: in3
  Multiplexer #(.select(2), .width(48)) multiplexer_6 (
    .in0({b1, g1, r1}), .in1({b2, g2, r2}), .in2({b3, g3, r3}), .out(multiplexer_6_out),
    .sel(sortfloats_1_order));  // open: in3
  // Probe on sortfloats_1_bottom
  Multiplexer #(.width(16)) multiplexer_7 (
    .in0(sortfloats_1_bottom), .in1(fpadder_1_out), .out(multiplexer_7_out), .sel(and_1_out));
  MaxFloat maxfloat_1 (.A(16'h5c00), .B(sortfloats_1_top), .Lower(maxfloat_1_lower));  // open: Higher
  // FPComparator #(.fpwidth(16)) fpcomparator_1: pin names not known; wires that end beside it: maxfloat_1_lower, fpcomparator_1_p2, fpcomparator_1_p3, fpcomparator_1_p4
  DotProduct dotproduct_1 (
    .X1(multiplexer_1_out[15:0]), .Y1(multiplexer_1_out[31:16]), .X2(multiplexer_3_out),
    .Y2(multiplexer_3_out_2), .X3(multiplexer_5_out), .Y3(multiplexer_5_out_2),
    .UpOriented(dotproduct_1_uporiented));  // open: Product
  Register #(.width(16)) register_1 (
    .D(multiplexer_7_out), .en(or_2_out), .Q(fpcomparator_1_p2), .clk(clock_1_out), .clr(RESET));
  or or_1 (or_1_out, fpcomparator_1_p3, fpcomparator_1_p4);
  // Probe on fpcomparator_1_p2
  Counter #(.max('h3), .ongoal("stay"), .width(2)) counter_1 (
    .count(Start), .carry(counter_1_carry), .clk(clock_1_out), .clr(RESET));  // open: load, D, Q, up
  not not_1 (not_1_out, dotproduct_1_uporiented);
  // Probe on fliptriangle_1_top_dest_pos[15:0]
  // Probe on fliptriangle_1_top_dest_pos[31:16]
  // Probe on fliptriangle_1_top_dest_pos_2
  Slope YTOP (
    .x1(fliptriangle_1_top_dest_pos[15:0]), .y1(fliptriangle_1_top_dest_pos[31:16]),
    .x2(fliptriangle_1_top_src_pos), .y2(fliptriangle_1_top_src_pos_2), .b(YTOP_b), .m(YTOP_m));
  Slope ZTOP (
    .x1(fliptriangle_1_top_dest_pos[15:0]), .y1(fliptriangle_1_top_dest_pos_2),
    .x2(fliptriangle_1_top_src_pos), .y2(fliptriangle_1_top_src_pos_3), .b(ZTOP_b), .m(ZTOP_m));
  Slope RTOP (
    .x1(fliptriangle_1_top_dest_pos[15:0]), .y1(fliptriangle_1_top_dest_color),
    .x2(fliptriangle_1_top_src_pos), .y2(fliptriangle_1_top_src_color), .b(RTOP_b), .m(RTOP_m));
  Slope GTOP (
    .x1(fliptriangle_1_top_dest_pos[15:0]), .y1(fliptriangle_1_top_dest_color_2),
    .x2(fliptriangle_1_top_src_pos), .y2(fliptriangle_1_top_src_color_2), .b(GTOP_b), .m(GTOP_m));
  Slope BTOP (
    .x1(fliptriangle_1_top_dest_pos[15:0]), .y1(fliptriangle_1_top_dest_color_3),
    .x2(fliptriangle_1_top_src_pos), .y2(fliptriangle_1_top_src_color_3), .b(BTOP_b), .m(BTOP_m));
  FPAdder #(.fpwidth(16)) fpadder_1 (.a(fpcomparator_1_p2), .b(16'h3c00), .out(fpadder_1_out));
  and and_1 (and_1_out, or_5_out, ~and_2_out);  // AND_Gate
  or or_2 (or_2_out, and_2_out, or_5_out);
  and and_2 (and_2_out, ~counter_1_carry, Start);  // AND_Gate
  FlipTriangle fliptriangle_1 (
    .Left_Pos(multiplexer_1_out), .Left_Color(multiplexer_2_out),
    .Middle_Pos({multiplexer_3_out_3, multiplexer_3_out_2, multiplexer_3_out}),
    .Middle_Color(multiplexer_4_out),
    .Right_Pos({multiplexer_5_out_3, multiplexer_5_out_2, multiplexer_5_out}),
    .Right_Color(multiplexer_6_out), .UpOriented(not_1_out), .Flip(fpcomparator_6_p3),
    .Top_Src_Pos({fliptriangle_1_top_src_pos_3, fliptriangle_1_top_src_pos_2, fliptriangle_1_top_src_pos}),
    .Top_Src_Color({fliptriangle_1_top_src_color_3, fliptriangle_1_top_src_color_2, fliptriangle_1_top_src_color}),
    .Top_Dest_Pos({fliptriangle_1_top_dest_pos_2, fliptriangle_1_top_dest_pos}),
    .Top_Dest_Color({fliptriangle_1_top_dest_color_3, fliptriangle_1_top_dest_color_2, fliptriangle_1_top_dest_color}),
    .Bottom_Src_Pos(fliptriangle_1_bottom_src_pos), .Bottom_Src_Color(fliptriangle_1_bottom_src_color),
    .Bottom_Dest_Pos(fliptriangle_1_bottom_dest_pos), .Bottom_Dest_Color(fliptriangle_1_bottom_dest_color));
  // Probe on YTOP_m
  and and_3 (RESET, or_1_out, counter_1_carry);
  // Probe on fliptriangle_1_bottom_dest_pos[31:16]
  // Probe on fliptriangle_1_bottom_dest_pos[47:32]
  Slope YBOTTOM (
    .x1(fliptriangle_1_bottom_dest_pos[15:0]), .y1(fliptriangle_1_bottom_dest_pos[31:16]),
    .x2(fliptriangle_1_bottom_src_pos[15:0]), .y2(fliptriangle_1_bottom_src_pos[31:16]), .b(YBOTTOM_b),
    .m(YBOTTOM_m));
  Slope ZBOTTOM (
    .x1(fliptriangle_1_bottom_dest_pos[15:0]), .y1(fliptriangle_1_bottom_dest_pos[47:32]),
    .x2(fliptriangle_1_bottom_src_pos[15:0]), .y2(fliptriangle_1_bottom_src_pos[47:32]), .b(ZBOTTOM_b),
    .m(ZBOTTOM_m));
  // Probe on fliptriangle_1_top_src_pos
  // Probe on fliptriangle_1_top_src_pos_2
  // Probe on fliptriangle_1_top_src_pos_3
  Slope RBOTTOM (
    .x1(fliptriangle_1_bottom_dest_pos[15:0]), .y1(fliptriangle_1_bottom_dest_color[15:0]),
    .x2(fliptriangle_1_bottom_src_pos[15:0]), .y2(fliptriangle_1_bottom_src_color[15:0]), .b(RBOTTOM_b),
    .m(RBOTTOM_m));
  Slope GBOTTOM (
    .x1(fliptriangle_1_bottom_dest_pos[15:0]), .y1(fliptriangle_1_bottom_dest_color[31:16]),
    .x2(fliptriangle_1_bottom_src_pos[15:0]), .y2(fliptriangle_1_bottom_src_color[31:16]), .b(GBOTTOM_b),
    .m(GBOTTOM_m));
  Slope BBOTTOM (
    .x1(fliptriangle_1_bottom_dest_pos[15:0]), .y1(fliptriangle_1_bottom_dest_color[47:32]),
    .x2(fliptriangle_1_bottom_src_pos[15:0]), .y2(fliptriangle_1_bottom_src_color[47:32]), .b(BBOTTOM_b),
    .m(BBOTTOM_m));
  // FPComparator #(.fpwidth(16)) fpcomparator_2: pin names not known; wires that end beside it: fliptriangle_1_bottom_dest_pos[15:0], YTOP_m, 16'h7c00
  // OR_Gate or_3 has open pins: out=or_3_out
  // FPComparator #(.fpwidth(16)) fpcomparator_3: pin names not known; wires that end beside it: 16'h7c00, YBOTTOM_m
  // FPComparator #(.fpwidth(16)) fpcomparator_4: pin names not known; wires that end beside it: YTOP_m, fpcomparator_4_p2
  // FPComparator #(.fpwidth(16)) fpcomparator_5: pin names not known; wires that end beside it: 16'hfc00, YBOTTOM_m, fpcomparator_5_p3
  // Probe on sortfloats_1_middle
  // FPComparator #(.fpwidth(16)) fpcomparator_6: pin names not known; wires that end beside it: sortfloats_1_middle, fpcomparator_1_p2, fpcomparator_6_p3
  LineEq lineeq_1 (.x(fpcomparator_1_p2), .m(YBOTTOM_m), .b(YBOTTOM_b), .y(lineeq_1_y));
  LineEq lineeq_2 (.x(fpcomparator_1_p2), .m(ZBOTTOM_m), .b(ZBOTTOM_b), .y(lineeq_2_y));
  LineEq lineeq_3 (.x(fpcomparator_1_p2), .m(RBOTTOM_m), .b(RBOTTOM_b), .y(lineeq_3_y));
  LineEq lineeq_4 (.x(fpcomparator_1_p2), .m(GBOTTOM_m), .b(GBOTTOM_b), .y(lineeq_4_y));
  LineEq lineeq_5 (.x(fpcomparator_1_p2), .m(BBOTTOM_m), .b(BBOTTOM_b), .y(lineeq_5_y));
  LineEq lineeq_6 (.x(fpcomparator_1_p2), .m(YTOP_m), .b(YTOP_b), .y(lineeq_6_y));
  LineEq lineeq_7 (.x(fpcomparator_1_p2), .m(ZTOP_m), .b(ZTOP_b), .y(lineeq_7_y));
  LineEq lineeq_8 (.x(fpcomparator_1_p2), .m(RTOP_m), .b(RTOP_b), .y(lineeq_8_y));
  LineEq lineeq_9 (.x(fpcomparator_1_p2), .m(GTOP_m), .b(GTOP_b), .y(lineeq_9_y));
  LineEq lineeq_10 (.x(fpcomparator_1_p2), .m(BTOP_m), .b(BTOP_b), .y(lineeq_10_y));
  or or_4 (or_4_out, fpcomparator_4_p2, or_3_out, fpcomparator_5_p3);
  // Probe on lineeq_1_y
  and and_4 (and_4_out, ~and_2_out, ~or_5_out);  // AND_Gate
  Multiplexer #(.width(16)) multiplexer_8 (
    .in0(lineeq_1_y), .in1(fpadder_2_out), .out(multiplexer_8_out), .sel(and_4_out));
  Register #(.width(16)) register_2 (
    .D(multiplexer_8_out), .Q(register_2_q), .clk(clock_1_out), .clr(RESET));  // open: en
  // Probe on lineeq_6_y
  FPAdder #(.fpwidth(16)) fpadder_2 (.a(register_2_q), .b(16'hbc00), .out(fpadder_2_out));
  Slope slope_1 (.x1(lineeq_1_y), .y1(lineeq_2_y), .x2(lineeq_6_y), .y2(lineeq_7_y), .b(slope_1_b), .m(slope_1_m));
  Slope slope_2 (.x1(lineeq_1_y), .y1(lineeq_3_y), .x2(lineeq_6_y), .y2(lineeq_8_y), .b(slope_2_b), .m(slope_2_m));
  Slope slope_3 (.x1(lineeq_1_y), .y1(lineeq_4_y), .x2(lineeq_6_y), .y2(lineeq_9_y), .b(slope_3_b), .m(slope_3_m));
  Slope slope_4 (.x1(lineeq_1_y), .y1(lineeq_5_y), .x2(lineeq_6_y), .y2(lineeq_10_y), .b(slope_4_b), .m(slope_4_m));
  LineEq lineeq_11 (.x(register_2_q), .m(slope_1_m), .b(slope_1_b), .y(lineeq_11_y));
  LineEq lineeq_12 (.x(register_2_q), .m(slope_2_m), .b(slope_2_b), .y(lineeq_12_y));
  MaxFloat maxfloat_2 (.A(lineeq_12_y), .B(16'h3c00), .Lower(maxfloat_2_lower));  // open: Higher
  LineEq lineeq_13 (.x(register_2_q), .m(slope_3_m), .b(slope_3_b), .y(lineeq_13_y));
  MaxFloat maxfloat_3 (.A(lineeq_13_y), .B(16'h3c00), .Lower(maxfloat_3_lower));  // open: Higher
  LineEq lineeq_14 (.x(register_2_q), .m(slope_4_m), .b(slope_4_b), .y(lineeq_14_y));
  MaxFloat maxfloat_4 (.A(lineeq_14_y), .B(16'h3c00), .Lower(maxfloat_4_lower));  // open: Higher
  // FPComparator #(.fpwidth(16)) fpcomparator_7: pin names not known; wires that end beside it: register_2_q, lineeq_6_y, fpcomparator_7_p3, fpcomparator_7_p4
  // Probe on fpcomparator_1_p2
  // Probe on register_2_q
  // Probe on lineeq_11_y
  MaxFloat maxfloat_5 (.A({16{1'b0}}), .B(maxfloat_2_lower), .Higher(maxfloat_5_higher));  // open: Lower
  MaxFloat maxfloat_6 (.A({16{1'b0}}), .B(maxfloat_3_lower), .Higher(maxfloat_6_higher));  // open: Lower
  MaxFloat maxfloat_7 (.A({16{1'b0}}), .B(maxfloat_4_lower), .Higher(maxfloat_7_higher));  // open: Lower
  or or_5 (or_5_out, or_4_out, fpcomparator_7_p3, fpcomparator_7_p4, or_6_out);
  // Probe on maxfloat_5_higher
  FPMultiplier #(.fpwidth(16)) fpmultiplier_1 (.a(maxfloat_5_higher), .b(16'h5bf8), .out(fpmultiplier_1_out));
  // Probe on maxfloat_6_higher
  FPMultiplier #(.fpwidth(16)) fpmultiplier_2 (.a(maxfloat_6_higher), .b(16'h5bf8), .out(fpmultiplier_2_out));
  // Probe on maxfloat_7_higher
  FPMultiplier #(.fpwidth(16)) fpmultiplier_3 (.a(maxfloat_7_higher), .b(16'h5bf8), .out(fpmultiplier_3_out));
  // FPComparator #(.fpwidth(16)) fpcomparator_8: pin names not known; wires that end beside it: {16{1'b0}}, fpcomparator_1_p2, fpcomparator_8_p3
  // FPComparator #(.fpwidth(16)) fpcomparator_9: pin names not known; wires that end beside it: 16'h5c00, register_2_q, fpcomparator_9_p3
  or or_6 (or_6_out, fpcomparator_8_p3, fpcomparator_9_p3, fpcomparator_10_p3);
  // FPComparator #(.fpwidth(16)) fpcomparator_10: pin names not known; wires that end beside it: {16{1'b0}}, register_2_q, fpcomparator_10_p3
  // FPToInt #(.fpwidth(16)) fptoint_1: pin names not known; wires that end beside it: fpcomparator_1_p2, x_out
  assign bit_extender_1_out = {{8{1'b0}}, x_out};  // Bit_Extender bit_extender_1
  // FPToInt #(.fpwidth(16)) fptoint_2: pin names not known; wires that end beside it: register_2_q, y_out
  RAM #(.addrWidth(16), .clearpin("true"), .dataWidth(16), .readbehav("war")) ZBuffer (
    .addr(adder_1_out), .we(or_7_out), .clk(clock_1_out), .din(lineeq_11_y), .dout(ZBuffer_dout),
    .clr(Clear_Buffer));  // open: oe
  // FPComparator #(.fpwidth(16)) fpcomparator_11: pin names not known; wires that end beside it: lineeq_11_y, ZBuffer_dout, fpcomparator_11_p3
  // FPToInt #(.fpwidth(16)) fptoint_3: pin names not known; wires that end beside it: fptoint_3_p1, fptoint_3_p1, fpmultiplier_1_out, rgb[7:0]
  // FPToInt #(.fpwidth(16)) fptoint_4: pin names not known; wires that end beside it: fpmultiplier_2_out, rgb[15:8]
  // FPToInt #(.fpwidth(16)) fptoint_5: pin names not known; wires that end beside it: fpmultiplier_3_out, rgb[23:16]
  Multiplier #(.width(16)) multiplier_1 (
    .a(bit_extender_1_out), .b(16'h100), .out(multiplier_1_out));  // open: cin, cout
  assign bit_extender_2_out = {{8{1'b0}}, y_out};  // Bit_Extender bit_extender_2
  Adder #(.width(16)) adder_1 (.a(multiplier_1_out), .b(bit_extender_2_out), .out(adder_1_out));  // open: cin, cout
  or or_7 (or_7_out, fpcomparator_11_p3, fpcomparator_12_p4);
  // FPComparator #(.fpwidth(16)) fpcomparator_12: pin names not known; wires that end beside it: {16{1'b0}}, ZBuffer_dout, or_7_out, fpcomparator_12_p4
  // Probe on ZBuffer_dout

  assign Write_Enable = 1'b1;
endmodule

module MaxFloat (
  input  [15:0] A,
  input  [15:0] B,
  output [15:0] Higher,
  output [15:0] Lower
);

  wire fpcomparator_1_p3, fpcomparator_1_p4, fpcomparator_1_p5, fpcomparator_1_p6;

  // FPComparator #(.fpwidth(16)) fpcomparator_1: pin names not known; wires that end beside it: A, B, fpcomparator_1_p3, fpcomparator_1_p4, fpcomparator_1_p5, fpcomparator_1_p6
  or or_1 (fpcomparator_1_p6, fpcomparator_1_p3, fpcomparator_1_p4);
  Multiplexer #(.width(16)) multiplexer_1 (.in0(A), .in1(B), .out(Lower), .sel(fpcomparator_1_p6));
  Multiplexer #(.width(16)) multiplexer_2 (.in0(A), .in1(B), .out(Higher), .sel(fpcomparator_1_p5));
endmodule

module FlipTriangle (
  input  [47:0] Left_Pos,
  input  [47:0] Left_Color,
  input  [47:0] Middle_Pos,
  input  [47:0] Middle_Color,
  input  [47:0] Right_Pos,
  input  [47:0] Right_Color,
  input  UpOriented,
  input  Flip,
  output [47:0] Top_Src_Pos,
  output [47:0] Top_Src_Color,
  output [47:0] Top_Dest_Pos,
  output [47:0] Top_Dest_Color,
  output [47:0] Bottom_Src_Pos,
  output [47:0] Bottom_Src_Color,
  output [47:0] Bottom_Dest_Pos,
  output [47:0] Bottom_Dest_Color
);

  wire and_1_out, and_2_out;
  wire [47:0] multiplexer_1_out, multiplexer_2_out, multiplexer_3_out, multiplexer_4_out, multiplexer_9_out,
       multiplexer_10_out, multiplexer_11_out, multiplexer_12_out, multiplexer_13_out, multiplexer_14_out,
       multiplexer_15_out, multiplexer_16_out;

  Multiplexer #(.width(48)) multiplexer_1 (
    .in0(Left_Pos), .in1(multiplexer_9_out), .out(multiplexer_1_out), .sel(UpOriented));
  Multiplexer #(.width(48)) multiplexer_2 (
    .in0(Left_Color), .in1(multiplexer_10_out), .out(multiplexer_2_out), .sel(UpOriented));
  Multiplexer #(.width(48)) multiplexer_3 (
    .in0(multiplexer_11_out), .in1(Left_Pos), .out(multiplexer_3_out), .sel(UpOriented));
  Multiplexer #(.width(48)) multiplexer_4 (
    .in0(multiplexer_12_out), .in1(Left_Color), .out(multiplexer_4_out), .sel(UpOriented));
  Multiplexer #(.width(48)) multiplexer_5 (.in0(Left_Pos), .in1(multiplexer_1_out), .out(Top_Src_Pos), .sel(Flip));
  Multiplexer #(.width(48)) multiplexer_6 (.in0(Left_Color), .in1(multiplexer_2_out), .out(Top_Src_Color), .sel(Flip));
  Multiplexer #(.width(48)) multiplexer_7 (.in0(Left_Pos), .in1(multiplexer_3_out), .out(Bottom_Src_Pos), .sel(Flip));
  Multiplexer #(.width(48)) multiplexer_8 (
    .in0(Left_Color), .in1(multiplexer_4_out), .out(Bottom_Src_Color), .sel(Flip));
  Multiplexer #(.width(48)) multiplexer_9 (
    .in0(Right_Pos), .in1(Middle_Pos), .out(multiplexer_9_out), .sel(UpOriented));
  Multiplexer #(.width(48)) multiplexer_10 (
    .in0(Right_Color), .in1(Middle_Color), .out(multiplexer_10_out), .sel(UpOriented));
  Multiplexer #(.width(48)) multiplexer_11 (
    .in0(Middle_Pos), .in1(Right_Pos), .out(multiplexer_11_out), .sel(UpOriented));
  Multiplexer #(.width(48)) multiplexer_12 (
    .in0(Middle_Color), .in1(Right_Color), .out(multiplexer_12_out), .sel(UpOriented));
  Multiplexer #(.width(48)) multiplexer_13 (
    .in0(Right_Pos), .in1(Middle_Pos), .out(multiplexer_13_out), .sel(UpOriented));
  Multiplexer #(.width(48)) multiplexer_14 (
    .in0(Right_Color), .in1(Middle_Color), .out(multiplexer_14_out), .sel(UpOriented));
  Multiplexer #(.width(48)) multiplexer_15 (
    .in0(Middle_Pos), .in1(Right_Pos), .out(multiplexer_15_out), .sel(UpOriented));
  Multiplexer #(.width(48)) multiplexer_16 (
    .in0(Middle_Color), .in1(Right_Color), .out(multiplexer_16_out), .sel(UpOriented));
  Multiplexer #(.width(48)) multiplexer_17 (
    .in0(multiplexer_9_out), .in1(multiplexer_15_out), .out(Top_Dest_Pos), .sel(and_2_out));
  Multiplexer #(.width(48)) multiplexer_18 (
    .in0(multiplexer_10_out), .in1(multiplexer_16_out), .out(Top_Dest_Color), .sel(and_2_out));
  Multiplexer #(.width(48)) multiplexer_19 (
    .in0(multiplexer_11_out), .in1(multiplexer_13_out), .out(Bottom_Dest_Pos), .sel(and_1_out));
  Multiplexer #(.width(48)) multiplexer_20 (
    .in0(multiplexer_12_out), .in1(multiplexer_14_out), .out(Bottom_Dest_Color), .sel(and_1_out));
  and and_1 (and_1_out, ~UpOriented, Flip);  // AND_Gate
  and and_2 (and_2_out, UpOriented, Flip);
endmodule
